// Logisim project Platformer.circ as structural Verilog: 30 circuits, main circuit Playground
module main (
);

  DotMatrix #(.matrixcols(32), .matrixrows(32)) dotmatrix_1 ();  // open: col0, col1, col2, col3, col4, col5, col6, col7, col8, col9, col10, col11, col12, col13, col14, col15, col16, col17, col18, col19, col20, col21, col22, col23, col24, col25, col26, col27, col28, col29, col30, col31
  // testPlate testplate_1: pin names not known
endmodule

module Level_Installer (
  input  [4:0] Number_of_column,
  input  [31:0] bus_0,
  input  [31:0] bus_1,
  input  [31:0] bus_2,
  input  [31:0] bus_3,
  input  [31:0] bus_4,
  input  [31:0] bus_5,
  input  [31:0] bus_6,
  input  [31:0] bus_7,
  input  [31:0] bus_8,
  input  [31:0] bus_9,
  input  [31:0] bus_10,
  input  [31:0] bus_11,
  input  [31:0] bus_12,
  input  [31:0] bus_13,
  input  [31:0] bus_14,
  input  [31:0] bus_15,
  input  [31:0] bus_16,
  input  [31:0] bus_17,
  input  [31:0] bus_18,
  input  [31:0] bus_19,
  input  [31:0] bus_20,
  input  [31:0] bus_21,
  input  [31:0] bus_22,
  input  [31:0] bus_23,
  input  [31:0] bus_24,
  input  [31:0] bus_25,
  input  [31:0] bus_26,
  input  [31:0] bus_27,
  input  [31:0] bus_28,
  input  [31:0] bus_29,
  input  [31:0] bus_30,
  input  [31:0] bus_31,
  output [31:0] Column
);

  Multiplexer #(.select(5), .width(32), .enable("false")) multiplexer_1 (
    .in0(bus_0), .in1(bus_1), .in2(bus_2), .in3(bus_3), .in4(bus_4), .in5(bus_5), .in6(bus_6), .in7(bus_7),
    .in8(bus_8), .in9(bus_9), .in10(bus_10), .in11(bus_11), .in12(bus_12), .in13(bus_13), .in14(bus_14),
    .in15(bus_15), .in16(bus_16), .in17(bus_17), .in18(bus_18), .in19(bus_19), .in20(bus_20), .in21(bus_21),
    .in22(bus_22), .in23(bus_23), .in24(bus_24), .in25(bus_25), .in26(bus_26), .in27(bus_27), .in28(bus_28),
    .in29(bus_29), .in30(bus_30), .in31(bus_31), .out(Column), .sel(Number_of_column));

  // Other names for the same wires on the sheet: _1[31:0] = bus_0; _2[31:0] = bus_1; _3[31:0] = bus_2;
  //   _4[31:0] = bus_3; _5[31:0] = bus_4; _6[31:0] = bus_5; _7[31:0] = bus_6; _8[31:0] = bus_7; _9[31:0] = bus_8;
  //   _10[31:0] = bus_9; _11[31:0] = bus_10; _12[31:0] = bus_11; _13[31:0] = bus_12; _14[31:0] = bus_13;
  //   _15[31:0] = bus_14; _16[31:0] = bus_15; _17[31:0] = bus_16; _18[31:0] = bus_17; _19[31:0] = bus_18;
  //   _20[31:0] = bus_19; _21[31:0] = bus_20; _22[31:0] = bus_21; _23[31:0] = bus_22; _24[31:0] = bus_23;
  //   _25[31:0] = bus_24; _26[31:0] = bus_25; _27[31:0] = bus_26; _28[31:0] = bus_27; _29[31:0] = bus_28;
  //   _30[31:0] = bus_29; _31[31:0] = bus_30; _32[31:0] = bus_31

  // Notes on the sheet:
  //   Level Installer
endmodule

module Levels_Storage (
  input  Clock,
  input  [4:0] Number_of_location,
  output [31:0] Column,
  output [4:0] Number_of_column,
  output [4:0] X___winTo,
  output [4:0] Y___winTo,
  output [4:0] X___winFrom,
  output [4:0] Y___winFrom,
  output [4:0] X___startFrom,
  output [4:0] Y___startFrom
);

  wire _1, _2, _3, _4, _5, _6, _7, _8, _9, _10, _11, _12, _13, _14, _15, _16, _17, _18, _19, _20, _21, _22,
       _23, _24, _25, _26, _27, _28, _29, _30, _31, _32, and_1_out, and_2_out, and_3_out, and_4_out,
       and_5_out, and_6_out, and_7_out, and_8_out, and_9_out, and_10_out, and_11_out;

  greetingScreen greetingscreen_1 (
    .Clock(and_1_out), .Number_of_column(Number_of_column), .Column(Column), .X___start(X___startFrom),
    .Y___start(Y___startFrom), .On_Off(_1), .X___finishTo(X___winTo), .Y___finishTo(Y___winTo),
    .X___finishFrom(X___winFrom), .Y___finishFrom(Y___winFrom));
  and and_1 (and_1_out, Clock, _1);
  _8location u_8location_1 (
    .Clock(and_2_out), .Number_of_column(Number_of_column), .Column(Column), .X___start(X___startFrom),
    .Y___start(Y___startFrom), .On_Off(_9), .X___finishTo(X___winTo), .Y___finishTo(Y___winTo),
    .X___finishFrom(X___winFrom), .Y___finishFrom(Y___winFrom));
  and and_2 (and_2_out, Clock, _9);
  Decoder #(.select(5), .enable("false")) decoder_1 (
    .out0(_1), .out1(_2), .out2(_3), .out3(_4), .out4(_5), .out5(_6), .out6(_7), .out7(_8), .out8(_9),
    .out9(_10), .out10(_11), .out11(_12), .out12(_13), .out13(_14), .out14(_15), .out15(_16), .out16(_17),
    .out17(_18), .out18(_19), .out19(_20), .out20(_21), .out21(_22), .out22(_23), .out23(_24), .out24(_25),
    .out25(_26), .out26(_27), .out27(_28), .out28(_29), .out29(_30), .out30(_31), .out31(_32),
    .sel(Number_of_location));
  firstLocation firstlocation_1 (
    .Clock(and_3_out), .Number_of_column(Number_of_column), .Column(Column), .X___start(X___startFrom),
    .Y___start(Y___startFrom), .On_Off(_2), .X___finishTo(X___winTo), .Y___finishTo(Y___winTo),
    .X___finishFrom(X___winFrom), .Y___finishFrom(Y___winFrom));
  and and_3 (and_3_out, Clock, _2);
  _9location u_9location_1 (
    .Clock(and_4_out), .Number_of_column(Number_of_column), .Column(Column), .X___start(X___startFrom),
    .Y___start(Y___startFrom), .On_Off(_10), .X___finishTo(X___winTo), .Y___finishTo(Y___winTo),
    .X___finishFrom(X___winFrom), .Y___finishFrom(Y___winFrom));
  and and_4 (and_4_out, Clock, _10);
  secondLocation secondlocation_1 (
    .Clock(and_5_out), .Number_of_column(Number_of_column), .Column(Column), .X___start(X___startFrom),
    .Y___start(Y___startFrom), .On_Off(_3), .X___finishTo(X___winTo), .Y___finishTo(Y___winTo),
    .X___finishFrom(X___winFrom), .Y___finishFrom(Y___winFrom));
  and and_5 (and_5_out, Clock, _3);
  and and_6 (and_6_out, Clock, _11);
  _10location u_10location_1 (
    .Clock(and_6_out), .Number_of_column(Number_of_column), .Column(Column), .X___start(X___startFrom),
    .Y___start(Y___startFrom), .On_Off(_11), .X___finishTo(X___winTo), .Y___finishTo(Y___winTo),
    .X___finishFrom(X___winFrom), .Y___finishFrom(Y___winFrom));
  and and_7 (and_7_out, Clock, _4);
  thirdLocation thirdlocation_1 (
    .Clock(and_7_out), .Number_of_column(Number_of_column), .Column(Column), .X___start(X___startFrom),
    .Y___start(Y___startFrom), .On_Off(_4), .X___finishTo(X___winTo), .Y___finishTo(Y___winTo),
    .X___finishFrom(X___winFrom), .Y___finishFrom(Y___winFrom));
  and and_8 (and_8_out, Clock, _5);
  _4location u_4location_1 (
    .Clock(and_8_out), .Number_of_column(Number_of_column), .Column(Column), .X___start(X___startFrom),
    .Y___start(Y___startFrom), .On_Off(_5), .X___finishTo(X___winTo), .Y___finishTo(Y___winTo),
    .X___finishFrom(X___winFrom), .Y___finishFrom(Y___winFrom));
  and and_9 (and_9_out, Clock, _6);
  _5location u_5location_1 (
    .Clock(and_9_out), .Number_of_column(Number_of_column), .Column(Column), .X___start(X___startFrom),
    .Y___start(Y___startFrom), .On_Off(_6), .X___finishTo(X___winTo), .Y___finishTo(Y___winTo),
    .X___finishFrom(X___winFrom), .Y___finishFrom(Y___winFrom));
  and and_10 (and_10_out, Clock, _7);
  _6location u_6location_1 (
    .Clock(and_10_out), .Number_of_column(Number_of_column), .Column(Column), .X___start(X___startFrom),
    .Y___start(Y___startFrom), .On_Off(_7), .X___finishTo(X___winTo), .Y___finishTo(Y___winTo),
    .X___finishFrom(X___winFrom), .Y___finishFrom(Y___winFrom));
  and and_11 (and_11_out, Clock, _8);
  _7location u_7location_1 (
    .Clock(and_11_out), .Number_of_column(Number_of_column), .Column(Column), .X___start(X___startFrom),
    .Y___start(Y___startFrom), .On_Off(_8), .X___finishTo(X___winTo), .Y___finishTo(Y___winTo),
    .X___finishFrom(X___winFrom), .Y___finishFrom(Y___winFrom));

  // Other names for the same wires on the sheet: num[4:0] = Number_of_column; X[4:0] = X___startFrom;
  //   X___finishFrom[4:0] = X___winFrom; X___finishTo[4:0] = X___winTo; Y[4:0] = Y___startFrom;
  //   Y___finishFrom[4:0] = Y___winFrom; Y___finishTo[4:0] = Y___winTo

  // Notes on the sheet:
  //   The bit that the decoder selects corresponds to the location number.
endmodule

module Playground (
);

  wire [1:0] joystick_1_x, joystick_1_y;
  wire [31:0] level_controller_1_out_3, level_controller_1_out_4, level_controller_1_out_5,
       level_controller_1_out_6, level_controller_1_out_7, level_controller_1_out_8,
       level_controller_1_out_9, level_controller_1_out_10, level_controller_1_out_11,
       level_controller_1_out_12, level_controller_1_out_13, level_controller_1_out_14,
       level_controller_1_out_15, level_controller_1_out_16, level_controller_1_out_17,
       level_controller_1_out_18, level_controller_1_out_19, level_controller_1_out_20,
       level_controller_1_out_21, level_controller_1_out_22, level_controller_1_out_23,
       level_controller_1_out_24, level_controller_1_out_25, level_controller_1_out_26,
       level_controller_1_out_27, level_controller_1_out_28, level_controller_1_out_29,
       level_controller_1_out_30, level_controller_1_out_31, level_controller_1_out_32,
       level_controller_1_out_33, level_controller_1_out_34;

  DotMatrix #(.matrixcols(32), .matrixrows(32)) dotmatrix_1 (
    .col0(level_controller_1_out_3), .col1(level_controller_1_out_4), .col2(level_controller_1_out_5),
    .col3(level_controller_1_out_6), .col4(level_controller_1_out_7), .col5(level_controller_1_out_8),
    .col6(level_controller_1_out_9), .col7(level_controller_1_out_10), .col8(level_controller_1_out_11),
    .col9(level_controller_1_out_12), .col10(level_controller_1_out_13), .col11(level_controller_1_out_14),
    .col12(level_controller_1_out_15), .col13(level_controller_1_out_16), .col14(level_controller_1_out_17),
    .col15(level_controller_1_out_18), .col16(level_controller_1_out_19), .col17(level_controller_1_out_20),
    .col18(level_controller_1_out_21), .col19(level_controller_1_out_22), .col20(level_controller_1_out_23),
    .col21(level_controller_1_out_24), .col22(level_controller_1_out_25), .col23(level_controller_1_out_26),
    .col24(level_controller_1_out_27), .col25(level_controller_1_out_28), .col26(level_controller_1_out_29),
    .col27(level_controller_1_out_30), .col28(level_controller_1_out_31), .col29(level_controller_1_out_32),
    .col30(level_controller_1_out_33), .col31(level_controller_1_out_34));
  Level_Controller level_controller_1 (
    .X___joystick(joystick_1_x), .Y___joystick(joystick_1_y), .out_3(level_controller_1_out_3),
    .out_4(level_controller_1_out_4), .out_5(level_controller_1_out_5), .out_6(level_controller_1_out_6),
    .out_7(level_controller_1_out_7), .out_8(level_controller_1_out_8), .out_9(level_controller_1_out_9),
    .out_10(level_controller_1_out_10), .out_11(level_controller_1_out_11),
    .out_12(level_controller_1_out_12), .out_13(level_controller_1_out_13),
    .out_14(level_controller_1_out_14), .out_15(level_controller_1_out_15),
    .out_16(level_controller_1_out_16), .out_17(level_controller_1_out_17),
    .out_18(level_controller_1_out_18), .out_19(level_controller_1_out_19),
    .out_20(level_controller_1_out_20), .out_21(level_controller_1_out_21),
    .out_22(level_controller_1_out_22), .out_23(level_controller_1_out_23),
    .out_24(level_controller_1_out_24), .out_25(level_controller_1_out_25),
    .out_26(level_controller_1_out_26), .out_27(level_controller_1_out_27),
    .out_28(level_controller_1_out_28), .out_29(level_controller_1_out_29),
    .out_30(level_controller_1_out_30), .out_31(level_controller_1_out_31),
    .out_32(level_controller_1_out_32), .out_33(level_controller_1_out_33), .out_34(level_controller_1_out_34));
  Joystick #(.bits(2)) joystick_1 (.x(joystick_1_x), .y(joystick_1_y));
endmodule

module Level_Controller (
  input  [1:0] X___joystick,
  input  [1:0] Y___joystick,
  output [31:0] out_3,
  output [31:0] out_4,
  output [31:0] out_5,
  output [31:0] out_6,
  output [31:0] out_7,
  output [31:0] out_8,
  output [31:0] out_9,
  output [31:0] out_10,
  output [31:0] out_11,
  output [31:0] out_12,
  output [31:0] out_13,
  output [31:0] out_14,
  output [31:0] out_15,
  output [31:0] out_16,
  output [31:0] out_17,
  output [31:0] out_18,
  output [31:0] out_19,
  output [31:0] out_20,
  output [31:0] out_21,
  output [31:0] out_22,
  output [31:0] out_23,
  output [31:0] out_24,
  output [31:0] out_25,
  output [31:0] out_26,
  output [31:0] out_27,
  output [31:0] out_28,
  output [31:0] out_29,
  output [31:0] out_30,
  output [31:0] out_31,
  output [31:0] out_32,
  output [31:0] out_33,
  output [31:0] out_34
);

  wire _1, _2, _3, _4, _5, _6, _7, _8, _9, _10, _11, _12, _13, _14, _15, _16, _17, _18, _19, _20, _21, _22,
       _23, _24, _25, _26, _27, _28, _29, _30, _31, _32, and_1_out, and_2_out, and_3_out, and_4_out,
       and_5_out, and_6_out, and_7_out, and_8_out, and_9_out, and_10_out, and_11_out, and_12_out, and_13_out,
       and_14_out, and_15_out, cdm_8_mark5_1_p1, cdm_8_mark5_1_p2, cdm_8_mark5_1_p4, cdm_8_mark5_1_p5,
       cdm_8_mark5_1_p7, cdm_8_mark5_1_p8, cdm_8_mark5_1_p9, cdm_8_mark5_1_p10, checkUnder, clck, code,
       comparator_1_eq, comparator_2_eq, comparator_3_eq, comparator_4_eq, comparator_5_eq, comparator_6_eq,
       controlled_buffer_1_out, controlled_buffer_2_out, counter_1_carry, data, GameState, I_Osel,
       In_Out_prime, mem, nand_1_out, nor_1_out, nor_2_out, not_1_out, not_2_out, not_3_out, not_4_out,
       not_5_out, not_6_out, not_7_out, not_8_out, not_9_out, not_10_out, or_1_out, or_2_out, or_3_out, RAM,
       storeToXY, take_n_bit_3_bus_0, take_n_bit_4_bus_0, take_n_bit_5_bus_0, take_n_bit_6_bus_0,
       take_n_bit_7_bus_0, take_n_bit_8_bus_0, winOrNot, X1, X2, X3, X4, X5, X6, X7, X8, X9, X10, X11, X12,
       X13, X14, X15, X16, X17, X18, X19, X20, X21, X22, X23, X24, X25, X26, X27, X28, X29, X30, X31, X32;
  wire [0:0] multiplexer_35_out, multiplexer_36_out, multiplexer_44_out, multiplexer_45_out,
       multiplexer_49_out, multiplexer_52_out, take_n_bit_2_bus_0;
  wire [1:0] X___joystick_q, Y___joystick_q;
  wire [4:0] adder_1_out, adder_2_out, adder_3_out, adder_4_out, levels_storage_1_number_of_column,
       multiplexer_6_out, multiplexer_7_out, Number_of_Location_q, subtractor_1_out, subtractor_2_out,
       subtractor_3_out, subtractor_4_out, X___start, X___winFrom, X___winTo, X_q, XS, Y___start,
       Y___winFrom, Y___winTo, Y_q, YS;
  wire [7:0] addr, cdm_8_mark5_1_p14, cdm_8_mark5_1_p15, I_Odat, multiplexer_2_out, multiplexer_3_out;
  wire [31:0] col, ex1, ex2, ex3, ex4, ex5, ex6, ex7, ex8, ex9, ex10, ex11, ex12, ex13, ex14, ex15, ex16,
       ex17, ex18, ex19, ex20, ex21, ex22, ex23, ex24, ex25, ex26, ex27, ex28, ex29, ex30, ex31, ex32,
       multiplexer_28_out, multiplexer_41_out, multiplexer_42_out, xor_1_out, xor_2_out, xor_3_out,
       xor_4_out, xor_5_out, xor_6_out, xor_7_out, xor_8_out, xor_9_out, xor_10_out, xor_11_out, xor_12_out,
       xor_13_out, xor_14_out, xor_15_out, xor_16_out, xor_17_out, xor_18_out, xor_19_out, xor_20_out,
       xor_21_out, xor_22_out, xor_23_out, xor_24_out, xor_25_out, xor_26_out, xor_27_out, xor_28_out,
       xor_29_out, xor_30_out, xor_31_out, xor_32_out, Y;

  Multiplexer #(.width(32), .enable("false")) multiplexer_1 (.in0(ex1), .in1(xor_1_out), .out(out_3), .sel(X1));
  assign xor_1_out = ex1 ^ Y;  // XOR_Gate xor_1, 32 bits wide
  not not_1 (not_1_out, In_Out_prime);
  Multiplexer #(.width(8), .enable("false")) multiplexer_2 (
    .in1(I_Odat), .out(multiplexer_2_out), .sel(not_1_out));  // open: in0
  not not_2 (not_2_out, In_Out_prime);
  Multiplexer #(.width(8), .enable("false")) multiplexer_3 (
    .in1(I_Odat), .out(multiplexer_3_out), .sel(not_2_out));  // open: in0
  Multiplexer #(.width(32), .enable("false")) multiplexer_4 (.in0(ex2), .in1(xor_2_out), .out(out_4), .sel(X2));
  assign xor_2_out = ex2 ^ Y;  // XOR_Gate xor_2, 32 bits wide
  // Probe on X___start
  not not_3 (not_3_out, GameState);
  // Probe on Y___start
  Register #(.width(2)) u_X___joystick (.D(X___joystick), .Q(X___joystick_q), .clk(clck));  // open: en, clr
  Multiplexer #(.width(32), .enable("false")) multiplexer_5 (.in0(ex3), .in1(xor_3_out), .out(out_5), .sel(X3));
  assign xor_3_out = ex3 ^ Y;  // XOR_Gate xor_3, 32 bits wide
  Multiplexer #(.width(5), .enable("false")) multiplexer_6 (
    .in0(multiplexer_2_out[4:0]), .in1(X___start), .out(multiplexer_6_out), .sel(not_3_out));
  assign controlled_buffer_1_out = In_Out_prime ? nor_1_out : 1'bz;  // Controlled_Buffer controlled_buffer_1
  nor nor_1 (nor_1_out, GameState, clck);
  Multiplexer #(.width(5), .enable("false")) multiplexer_7 (
    .in0(multiplexer_3_out[4:0]), .in1(Y___start), .out(multiplexer_7_out), .sel(not_4_out));
  assign controlled_buffer_2_out = In_Out_prime ? nor_2_out : 1'bz;  // Controlled_Buffer controlled_buffer_2
  nor nor_2 (nor_2_out, GameState, clck);
  not not_4 (not_4_out, GameState);
  and and_1 (and_1_out, In_Out_prime, I_Osel, ~addr[0], ~addr[1], ~addr[2], ~addr[3]);  // AND_Gate
  Multiplexer #(.width(32), .enable("false")) multiplexer_8 (.in0(ex4), .in1(xor_4_out), .out(out_6), .sel(X4));
  assign xor_4_out = ex4 ^ Y;  // XOR_Gate xor_4, 32 bits wide
  Register #(.width(5)) X (.D(multiplexer_6_out), .Q(X_q), .clk(controlled_buffer_1_out));  // open: en, clr
  assign controlled_buffer_1_out = not_5_out ? and_2_out : 1'bz;  // Controlled_Buffer controlled_buffer_3
  not not_5 (not_5_out, In_Out_prime);
  and and_2 (and_2_out, I_Osel, ~addr[0], addr[1], ~addr[2], ~addr[3]);  // AND_Gate
  Register #(.width(5)) u_Y (.D(multiplexer_7_out), .Q(Y_q), .clk(controlled_buffer_2_out));  // open: en, clr
  assign controlled_buffer_2_out = not_6_out ? and_3_out : 1'bz;  // Controlled_Buffer controlled_buffer_4
  not not_6 (not_6_out, In_Out_prime);
  and and_3 (and_3_out, I_Osel, addr[0], addr[1], ~addr[2], ~addr[3]);  // AND_Gate
  Multiplexer #(.width(8), .enable("false")) multiplexer_9 (
    .in1({{6{1'b0}}, X___joystick_q}), .out(I_Odat), .sel(and_1_out));  // open: in0
  Multiplexer #(.width(32), .enable("false")) multiplexer_10 (.in0(ex5), .in1(xor_5_out), .out(out_7), .sel(X5));
  // Probe on X_q
  Multiplexer #(.width(8)) multiplexer_11 (
    .in1({3'b000, X_q}), .out(I_Odat), .sel(In_Out_prime), .en(and_2_out));  // open: in0
  // Probe on Y_q
  Multiplexer #(.width(8)) multiplexer_12 (
    .in1({3'b000, Y_q}), .out(I_Odat), .sel(In_Out_prime), .en(and_3_out));  // open: in0
  assign xor_5_out = ex5 ^ Y;  // XOR_Gate xor_5, 32 bits wide
  Register #(.width(2)) u_Y___joystick (.D(Y___joystick), .Q(Y___joystick_q), .clk(clck));  // open: en, clr
  Multiplexer #(.width(32), .enable("false")) multiplexer_13 (.in0(ex6), .in1(xor_6_out), .out(out_8), .sel(X6));
  assign xor_6_out = ex6 ^ Y;  // XOR_Gate xor_6, 32 bits wide
  Register #(.width(5)) X_to_Location (.D(X_q), .Q(XS), .clk(storeToXY));  // open: en, clr
  Register #(.width(5)) Y_to_Location (.D(Y_q), .Q(YS), .clk(storeToXY));  // open: en, clr
  Multiplexer #(.width(32), .enable("false")) multiplexer_14 (.in0(ex7), .in1(xor_7_out), .out(out_9), .sel(X7));
  assign xor_7_out = ex7 ^ Y;  // XOR_Gate xor_7, 32 bits wide
  Decoder #(.select(5), .enable("false")) decoder_1 (
    .out0(X1), .out1(X2), .out2(X3), .out3(X4), .out4(X5), .out5(X6), .out6(X7), .out7(X8), .out8(X9),
    .out9(X10), .out10(X11), .out11(X12), .out12(X13), .out13(X14), .out14(X15), .out15(X16), .out16(X17),
    .out17(X18), .out18(X19), .out19(X20), .out20(X21), .out21(X22), .out22(X23), .out23(X24), .out24(X25),
    .out25(X26), .out26(X27), .out27(X28), .out28(X29), .out29(X30), .out30(X31), .out31(X32), .sel(XS));
  Multiplexer #(.width(8), .enable("false")) multiplexer_15 (
    .in1({{6{1'b0}}, Y___joystick_q}), .out(I_Odat), .sel(and_4_out));  // open: in0
  and and_4 (and_4_out, In_Out_prime, I_Osel, addr[0], ~addr[1], ~addr[2], ~addr[3]);  // AND_Gate
  Multiplexer #(.width(32), .enable("false")) multiplexer_16 (.in0(ex8), .in1(xor_8_out), .out(out_10), .sel(X8));
  assign xor_8_out = ex8 ^ Y;  // XOR_Gate xor_8, 32 bits wide
  N_shift_of_1 n_shift_of_1_1 (.N(YS), .\output (Y));
  Multiplexer #(.width(32), .enable("false")) multiplexer_17 (.in0(ex9), .in1(xor_9_out), .out(out_11), .sel(X9));
  assign xor_9_out = ex9 ^ Y;  // XOR_Gate xor_9, 32 bits wide
  Multiplexer #(.width(32), .enable("false")) multiplexer_18 (.in0(ex10), .in1(xor_10_out), .out(out_12), .sel(X10));
  assign xor_10_out = ex10 ^ Y;  // XOR_Gate xor_10, 32 bits wide
  Multiplexer #(.width(32), .enable("false")) multiplexer_19 (.in0(ex11), .in1(xor_11_out), .out(out_13), .sel(X11));
  assign xor_11_out = ex11 ^ Y;  // XOR_Gate xor_11, 32 bits wide
  not not_7 (not_7_out, GameState);
  and and_5 (and_5_out, not_7_out, not_8_out);
  not not_8 (not_8_out, clck);
  Multiplexer #(.width(32), .enable("false")) multiplexer_20 (.in0(ex12), .in1(xor_12_out), .out(out_14), .sel(X12));
  assign xor_12_out = ex12 ^ Y;  // XOR_Gate xor_12, 32 bits wide
  Counter #(.width(1), .max('h1)) u_GameState (
    .count(or_1_out), .Q(GameState), .clk(or_1_out));  // open: load, D, carry, clr
  or or_1 (or_1_out, winOrNot, and_5_out);
  Counter #(.width(5), .max('h1f)) Number_of_Location (
    .count(winOrNot), .Q(Number_of_Location_q), .clk(winOrNot));  // open: load, D, carry, clr
  Multiplexer #(.width(32), .enable("false")) multiplexer_21 (.in0(ex13), .in1(xor_13_out), .out(out_15), .sel(X13));
  Multiplexer #(.width(8), .enable("false")) multiplexer_22 (
    .in1({3'b000, X___start}), .out(I_Odat), .sel(and_6_out));  // open: in0
  and and_6 (and_6_out, In_Out_prime, I_Osel, ~addr[0], ~addr[1], addr[2], addr[3]);  // AND_Gate
  assign xor_13_out = ex13 ^ Y;  // XOR_Gate xor_13, 32 bits wide
  // Probe on XS
  Multiplexer #(.width(32), .enable("false")) multiplexer_23 (.in0(ex14), .in1(xor_14_out), .out(out_16), .sel(X14));
  assign xor_14_out = ex14 ^ Y;  // XOR_Gate xor_14, 32 bits wide
  Subtractor #(.width(5)) subtractor_1 (.a(YS), .b(5'b00001), .out(subtractor_1_out));  // open: bin, bout
  Take_N_bit take_n_bit_1 (.Input(multiplexer_28_out), .N(subtractor_1_out), .bus_0(checkUnder));
  Decoder #(.select(5), .enable("false")) decoder_2 (
    .out0(_1), .out1(_2), .out2(_3), .out3(_4), .out4(_5), .out5(_6), .out6(_7), .out7(_8), .out8(_9),
    .out9(_10), .out10(_11), .out11(_12), .out12(_13), .out13(_14), .out14(_15), .out15(_16), .out16(_17),
    .out17(_18), .out18(_19), .out19(_20), .out20(_21), .out21(_22), .out22(_23), .out23(_24), .out24(_25),
    .out25(_26), .out26(_27), .out27(_28), .out28(_29), .out29(_30), .out30(_31), .out31(_32),
    .sel(levels_storage_1_number_of_column));
  Levels_Storage levels_storage_1 (
    .Clock(clck), .Number_of_location(Number_of_Location_q), .X___winFrom(X___winFrom),
    .Y___winFrom(Y___winFrom), .Column(col), .Number_of_column(levels_storage_1_number_of_column),
    .X___startFrom(X___start), .Y___startFrom(Y___start), .X___winTo(X___winTo), .Y___winTo(Y___winTo));
  Multiplexer #(.width(32), .enable("false")) multiplexer_24 (.in0(ex15), .in1(xor_15_out), .out(out_17), .sel(X15));
  assign xor_15_out = ex15 ^ Y;  // XOR_Gate xor_15, 32 bits wide
  Multiplexer #(.width(8), .enable("false")) multiplexer_25 (
    .in1({{7{1'b0}}, checkUnder}), .out(I_Odat), .sel(and_7_out));  // open: in0
  and and_7 (and_7_out, In_Out_prime, I_Osel, ~addr[0], addr[1], addr[2], ~addr[3]);  // AND_Gate
  Multiplexer #(.width(8), .enable("false")) multiplexer_26 (
    .in1({3'b000, Y___start}), .out(I_Odat), .sel(and_8_out));  // open: in0
  and and_8 (and_8_out, In_Out_prime, I_Osel, addr[0], ~addr[1], addr[2], addr[3]);  // AND_Gate
  Multiplexer #(.width(32), .enable("false")) multiplexer_27 (.in0(ex16), .in1(xor_16_out), .out(out_18), .sel(X16));
  assign xor_16_out = ex16 ^ Y;  // XOR_Gate xor_16, 32 bits wide
  Multiplexer #(.select(5), .width(32), .enable("false")) multiplexer_28 (
    .in0(out_3), .in1(out_4), .in2(out_5), .in3(out_6), .in4(out_7), .in5(out_8), .in6(out_9), .in7(out_10),
    .in8(out_11), .in9(out_12), .in10(out_13), .in11(out_14), .in12(out_15), .in13(out_16), .in14(out_17),
    .in15(out_18), .in16(out_19), .in17(out_20), .in18(out_21), .in19(out_22), .in20(out_23), .in21(out_24),
    .in22(out_25), .in23(out_26), .in24(out_27), .in25(out_28), .in26(out_29), .in27(out_30), .in28(out_31),
    .in29(out_32), .in30(out_33), .in31(out_34), .out(multiplexer_28_out), .sel(XS));
  Multiplexer #(.width(32), .enable("false")) multiplexer_29 (.in0(ex17), .in1(xor_17_out), .out(out_19), .sel(X17));
  Adder #(.width(5)) adder_1 (.a(YS), .b(5'b00001), .out(adder_1_out));  // open: cin, cout
  Take_N_bit take_n_bit_2 (.Input(multiplexer_28_out), .N(adder_1_out), .bus_0(take_n_bit_2_bus_0[0]));
  assign xor_17_out = ex17 ^ Y;  // XOR_Gate xor_17, 32 bits wide
  Multiplexer #(.width(8), .enable("false")) multiplexer_30 (
    .in1({{7{1'b0}}, take_n_bit_2_bus_0[0]}), .out(I_Odat), .sel(and_9_out));  // open: in0
  and and_9 (and_9_out, In_Out_prime, I_Osel, ~addr[0], addr[1], ~addr[2], addr[3]);  // AND_Gate
  Multiplexer #(.width(32), .enable("false")) multiplexer_31 (.in0(ex18), .in1(xor_18_out), .out(out_20), .sel(X18));
  assign xor_18_out = ex18 ^ Y;  // XOR_Gate xor_18, 32 bits wide
  Multiplexer #(.width(32), .enable("false")) multiplexer_32 (.in0(ex19), .in1(xor_19_out), .out(out_21), .sel(X19));
  assign xor_19_out = ex19 ^ Y;  // XOR_Gate xor_19, 32 bits wide
  Win_or_not win_or_not_1 (
    .X___winFrom(X___winFrom), .Y___winFrom(Y___winFrom), .X___winTo(X___winTo), .Y___winTo(Y___winTo),
    .X(XS), .Y(YS), ._1___win_0___not(winOrNot));
  Multiplexer #(.width(32), .enable("false")) multiplexer_33 (.in0(ex20), .in1(xor_20_out), .out(out_22), .sel(X20));
  assign xor_20_out = ex20 ^ Y;  // XOR_Gate xor_20, 32 bits wide
  Multiplexer #(.width(32), .enable("false")) multiplexer_34 (.in0(ex21), .in1(xor_21_out), .out(out_23), .sel(X21));
  Subtractor #(.width(5)) subtractor_2 (.a(XS), .b(5'b00001), .out(subtractor_2_out));  // open: bin, bout
  Comparator #(.width(5)) comparator_1 (.a(XS), .b({5{1'b0}}), .eq(comparator_1_eq));  // open: gt, lt
  // Probe on adder_2_out
  Adder #(.width(5)) adder_2 (.a(XS), .b(5'b00001), .out(adder_2_out));  // open: cin, cout
  Comparator #(.width(5)) comparator_2 (.a(XS), .b({5{1'b0}}), .eq(comparator_2_eq));  // open: gt, lt
  assign xor_21_out = ex21 ^ Y;  // XOR_Gate xor_21, 32 bits wide
  // Probe on subtractor_2_out
  Subtractor #(.width(5)) subtractor_3 (.a(YS), .b(5'b00001), .out(subtractor_3_out));  // open: bin, bout
  Take_N_bit take_n_bit_3 (.Input(multiplexer_41_out), .N(subtractor_3_out), .bus_0(take_n_bit_3_bus_0));
  or or_2 (or_2_out, comparator_1_eq, checkUnder);
  Multiplexer #(.enable("false")) multiplexer_35 (
    .in0(take_n_bit_3_bus_0), .in1(1'b1), .out(multiplexer_35_out[0]), .sel(or_2_out));
  Subtractor #(.width(5)) subtractor_4 (.a(YS), .b(5'b00001), .out(subtractor_4_out));  // open: bin, bout
  Take_N_bit take_n_bit_4 (.Input(multiplexer_42_out), .N(subtractor_4_out), .bus_0(take_n_bit_4_bus_0));
  or or_3 (or_3_out, comparator_2_eq, checkUnder);
  Multiplexer #(.enable("false")) multiplexer_36 (
    .in0(take_n_bit_4_bus_0), .in1(1'b1), .out(multiplexer_36_out[0]), .sel(or_3_out));
  Multiplexer #(.width(32), .enable("false")) multiplexer_37 (.in0(ex22), .in1(xor_22_out), .out(out_24), .sel(X22));
  assign xor_22_out = ex22 ^ Y;  // XOR_Gate xor_22, 32 bits wide
  Multiplexer #(.width(8), .enable("false")) multiplexer_38 (
    .in1({{7{1'b0}}, multiplexer_35_out[0]}), .out(I_Odat), .sel(and_10_out));  // open: in0
  and and_10 (and_10_out, In_Out_prime, I_Osel, addr[0], ~addr[1], addr[2], ~addr[3]);  // AND_Gate
  Multiplexer #(.width(8), .enable("false")) multiplexer_39 (
    .in1({{7{1'b0}}, multiplexer_36_out[0]}), .out(I_Odat), .sel(and_11_out));  // open: in0
  and and_11 (and_11_out, In_Out_prime, I_Osel, addr[0], addr[1], addr[2], ~addr[3]);  // AND_Gate
  Multiplexer #(.width(32), .enable("false")) multiplexer_40 (.in0(ex23), .in1(xor_23_out), .out(out_25), .sel(X23));
  assign xor_23_out = ex23 ^ Y;  // XOR_Gate xor_23, 32 bits wide
  Multiplexer #(.select(5), .width(32), .enable("false")) multiplexer_41 (
    .in0(out_3), .in1(out_4), .in2(out_5), .in3(out_6), .in4(out_7), .in5(out_8), .in6(out_9), .in7(out_10),
    .in8(out_11), .in9(out_12), .in10(out_13), .in11(out_14), .in12(out_15), .in13(out_16), .in14(out_17),
    .in15(out_18), .in16(out_19), .in17(out_20), .in18(out_21), .in19(out_22), .in20(out_23), .in21(out_24),
    .in22(out_25), .in23(out_26), .in24(out_27), .in25(out_28), .in26(out_29), .in27(out_30), .in28(out_31),
    .in29(out_32), .in30(out_33), .in31(out_34), .out(multiplexer_41_out), .sel(subtractor_2_out));
  Adder #(.width(5)) adder_3 (.a(YS), .b(5'b00001), .out(adder_3_out));  // open: cin, cout
  Take_N_bit take_n_bit_5 (.Input(multiplexer_41_out), .N(adder_3_out), .bus_0(take_n_bit_5_bus_0));
  Comparator #(.width(5)) comparator_3 (.a(XS), .b({5{1'b0}}), .eq(comparator_3_eq));  // open: gt, lt
  Multiplexer #(.select(5), .width(32), .enable("false")) multiplexer_42 (
    .in0(out_3), .in1(out_4), .in2(out_5), .in3(out_6), .in4(out_7), .in5(out_8), .in6(out_9), .in7(out_10),
    .in8(out_11), .in9(out_12), .in10(out_13), .in11(out_14), .in12(out_15), .in13(out_16), .in14(out_17),
    .in15(out_18), .in16(out_19), .in17(out_20), .in18(out_21), .in19(out_22), .in20(out_23), .in21(out_24),
    .in22(out_25), .in23(out_26), .in24(out_27), .in25(out_28), .in26(out_29), .in27(out_30), .in28(out_31),
    .in29(out_32), .in30(out_33), .in31(out_34), .out(multiplexer_42_out), .sel(adder_2_out));
  Comparator #(.width(5)) comparator_4 (.a(XS), .b({5{1'b1}}), .eq(comparator_4_eq));  // open: gt, lt
  Multiplexer #(.width(32), .enable("false")) multiplexer_43 (.in0(ex24), .in1(xor_24_out), .out(out_26), .sel(X24));
  assign xor_24_out = ex24 ^ Y;  // XOR_Gate xor_24, 32 bits wide
  Multiplexer #(.enable("false")) multiplexer_44 (
    .in0(take_n_bit_5_bus_0), .in1(1'b1), .out(multiplexer_44_out[0]), .sel(comparator_3_eq));
  and and_12 (and_12_out, In_Out_prime, I_Osel, addr[0], addr[1], ~addr[2], addr[3]);  // AND_Gate
  Adder #(.width(5)) adder_4 (.a(YS), .b(5'b00001), .out(adder_4_out));  // open: cin, cout
  Take_N_bit take_n_bit_6 (.Input(multiplexer_42_out), .N(adder_4_out), .bus_0(take_n_bit_6_bus_0));
  Multiplexer #(.enable("false")) multiplexer_45 (
    .in0(take_n_bit_6_bus_0), .in1(1'b1), .out(multiplexer_45_out[0]), .sel(comparator_4_eq));
  Multiplexer #(.width(32), .enable("false")) multiplexer_46 (.in0(ex25), .in1(xor_25_out), .out(out_27), .sel(X25));
  Multiplexer #(.width(8), .enable("false")) multiplexer_47 (
    .in1({{7{1'b0}}, multiplexer_44_out[0]}), .out(I_Odat), .sel(and_12_out));  // open: in0
  Multiplexer #(.width(8), .enable("false")) multiplexer_48 (
    .in1({{7{1'b0}}, multiplexer_45_out[0]}), .out(I_Odat), .sel(and_13_out));  // open: in0
  and and_13 (and_13_out, In_Out_prime, I_Osel, addr[0], ~addr[1], ~addr[2], addr[3]);  // AND_Gate
  assign xor_25_out = ex25 ^ Y;  // XOR_Gate xor_25, 32 bits wide
  Take_N_bit take_n_bit_7 (.Input(multiplexer_41_out), .N(YS), .bus_0(take_n_bit_7_bus_0));
  Comparator #(.width(5)) comparator_5 (.a(XS), .b({5{1'b0}}), .eq(comparator_5_eq));  // open: gt, lt
  Multiplexer #(.enable("false")) multiplexer_49 (
    .in0(take_n_bit_7_bus_0), .in1(1'b1), .out(multiplexer_49_out[0]), .sel(comparator_5_eq));
  Comparator #(.width(5)) comparator_6 (.a(XS), .b({5{1'b1}}), .eq(comparator_6_eq));  // open: gt, lt
  Multiplexer #(.width(32), .enable("false")) multiplexer_50 (.in0(ex26), .in1(xor_26_out), .out(out_28), .sel(X26));
  assign xor_26_out = ex26 ^ Y;  // XOR_Gate xor_26, 32 bits wide
  Multiplexer #(.width(8), .enable("false")) multiplexer_51 (
    .in1({{7{1'b0}}, multiplexer_49_out[0]}), .out(I_Odat), .sel(and_14_out));  // open: in0
  and and_14 (and_14_out, In_Out_prime, I_Osel, ~addr[0], ~addr[1], addr[2], ~addr[3]);  // AND_Gate
  Take_N_bit take_n_bit_8 (.Input(multiplexer_42_out), .N(YS), .bus_0(take_n_bit_8_bus_0));
  Multiplexer #(.enable("false")) multiplexer_52 (
    .in0(take_n_bit_8_bus_0), .in1(1'b1), .out(multiplexer_52_out[0]), .sel(comparator_6_eq));
  Multiplexer #(.width(32), .enable("false")) multiplexer_53 (.in0(ex27), .in1(xor_27_out), .out(out_29), .sel(X27));
  assign xor_27_out = ex27 ^ Y;  // XOR_Gate xor_27, 32 bits wide
  Multiplexer #(.width(8), .enable("false")) multiplexer_54 (
    .in1({{7{1'b0}}, multiplexer_52_out[0]}), .out(I_Odat), .sel(and_15_out));  // open: in0
  and and_15 (and_15_out, In_Out_prime, I_Osel, ~addr[0], ~addr[1], ~addr[2], addr[3]);  // AND_Gate
  Multiplexer #(.width(32), .enable("false")) multiplexer_55 (.in0(ex28), .in1(xor_28_out), .out(out_30), .sel(X28));
  assign xor_28_out = ex28 ^ Y;  // XOR_Gate xor_28, 32 bits wide
  Multiplexer #(.width(32), .enable("false")) multiplexer_56 (.in0(ex29), .in1(xor_29_out), .out(out_31), .sel(X29));
  assign xor_29_out = ex29 ^ Y;  // XOR_Gate xor_29, 32 bits wide
  Multiplexer #(.width(32), .enable("false")) multiplexer_57 (.in0(ex30), .in1(xor_30_out), .out(out_32), .sel(X30));
  assign xor_30_out = ex30 ^ Y;  // XOR_Gate xor_30, 32 bits wide
  Register #(.width(32)) register_1 (.D(col), .en(_1), .Q(ex1), .clk(clck));  // open: clr
  Register #(.width(32)) register_2 (.D(col), .en(_9), .Q(ex9), .clk(clck));  // open: clr
  Register #(.width(32)) register_3 (.D(col), .en(_17), .Q(ex17), .clk(clck));  // open: clr
  Register #(.width(32)) register_4 (.D(col), .en(_25), .Q(ex25), .clk(clck));  // open: clr
  Clock clock_1 (.out(clck));
  Multiplexer #(.width(32), .enable("false")) multiplexer_58 (.in0(ex31), .in1(xor_31_out), .out(out_33), .sel(X31));
  assign xor_31_out = ex31 ^ Y;  // XOR_Gate xor_31, 32 bits wide
  Counter #(.width(7), .max('h7f)) counter_1 (
    .count(clck), .carry(counter_1_carry), .clk(clck), .clr(winOrNot));  // open: load, D, Q
  Multiplexer #(.width(32), .enable("false")) multiplexer_59 (.in0(ex32), .in1(xor_32_out), .out(out_34), .sel(X32));
  assign xor_32_out = ex32 ^ Y;  // XOR_Gate xor_32, 32 bits wide
  Register #(.width(32)) register_5 (.D(col), .en(_2), .Q(ex2), .clk(clck));  // open: clr
  Register #(.width(32)) register_6 (.D(col), .en(_10), .Q(ex10), .clk(clck));  // open: clr
  Register #(.width(32)) register_7 (.D(col), .en(_18), .Q(ex18), .clk(clck));  // open: clr
  Register #(.width(32)) register_8 (.D(col), .en(_26), .Q(ex26), .clk(clck));  // open: clr
  or or_4 (storeToXY, counter_1_carry, winOrNot);
  and and_16 (I_Osel, not_9_out, clck, data);
  Register #(.width(32)) register_9 (.D(col), .en(_3), .Q(ex3), .clk(clck));  // open: clr
  Register #(.width(32)) register_10 (.D(col), .en(_11), .Q(ex11), .clk(clck));  // open: clr
  Register #(.width(32)) register_11 (.D(col), .en(_19), .Q(ex19), .clk(clck));  // open: clr
  Register #(.width(32)) register_12 (.D(col), .en(_27), .Q(ex27), .clk(clck));  // open: clr
  // Probe on cdm_8_mark5_1_p5
  // Probe on cdm_8_mark5_1_p4
  // Probe on cdm_8_mark5_1_p2
  // Probe on cdm_8_mark5_1_p1
  // Probe on cdm_8_mark5_1_p8
  // Probe on cdm_8_mark5_1_p9
  // Probe on cdm_8_mark5_1_p7
  // CdM_8_mark5 cdm_8_mark5_1: pin names not known; wires that end beside it: cdm_8_mark5_1_p1, cdm_8_mark5_1_p2, clck, cdm_8_mark5_1_p4, cdm_8_mark5_1_p5, storeToXY, cdm_8_mark5_1_p7, cdm_8_mark5_1_p8, cdm_8_mark5_1_p9, cdm_8_mark5_1_p10, mem, In_Out_prime, addr, cdm_8_mark5_1_p14, cdm_8_mark5_1_p15
  Button Reset ();  // open: out
  not not_9 (not_9_out, nand_1_out);
  nand nand_1 (nand_1_out, addr[4], addr[5], addr[6], addr[7]);
  and and_17 (RAM, nand_1_out, data);
  Register #(.width(32)) register_13 (.D(col), .en(_4), .Q(ex4), .clk(clck));  // open: clr
  Register #(.width(32)) register_14 (.D(col), .en(_12), .Q(ex12), .clk(clck));  // open: clr
  Register #(.width(32)) register_15 (.D(col), .en(_20), .Q(ex20), .clk(clck));  // open: clr
  Register #(.width(32)) register_16 (.D(col), .en(_28), .Q(ex28), .clk(clck));  // open: clr
  Decoder #(.disabled(0)) decoder_3 (.out0(code), .out1(data), .sel(cdm_8_mark5_1_p10), .en(mem));
  assign I_Odat = not_10_out ? cdm_8_mark5_1_p14 : 8'bz;  // Controlled_Buffer controlled_buffer_5
  not not_10 (not_10_out, In_Out_prime);
  assign cdm_8_mark5_1_p15 = In_Out_prime ? I_Odat : 8'bz;  // Controlled_Buffer controlled_buffer_6
  Register #(.width(32)) register_17 (.D(col), .en(_5), .Q(ex5), .clk(clck));  // open: clr
  Register #(.width(32)) register_18 (.D(col), .en(_13), .Q(ex13), .clk(clck));  // open: clr
  Register #(.width(32)) register_19 (.D(col), .en(_21), .Q(ex21), .clk(clck));  // open: clr
  Register #(.width(32)) register_20 (.D(col), .en(_29), .Q(ex29), .clk(clck));  // open: clr
  Register #(.width(32)) register_21 (.D(col), .en(_6), .Q(ex6), .clk(clck));  // open: clr
  Register #(.width(32)) register_22 (.D(col), .en(_14), .Q(ex14), .clk(clck));  // open: clr
  Register #(.width(32)) register_23 (.D(col), .en(_22), .Q(ex22), .clk(clck));  // open: clr
  Register #(.width(32)) register_24 (.D(col), .en(_30), .Q(ex30), .clk(clck));  // open: clr
  RAM ram_1 (.addr(addr), .data(I_Odat), .sel(RAM), .clk(clck), .ld(In_Out_prime));  // open: clr
  ROM rom_1 (.addr(addr), .data(I_Odat), .sel(code));
  Register #(.width(32)) register_25 (.D(col), .en(_7), .Q(ex7), .clk(clck));  // open: clr
  Register #(.width(32)) register_26 (.D(col), .en(_15), .Q(ex15), .clk(clck));  // open: clr
  Register #(.width(32)) register_27 (.D(col), .en(_23), .Q(ex23), .clk(clck));  // open: clr
  Register #(.width(32)) register_28 (.D(col), .en(_31), .Q(ex31), .clk(clck));  // open: clr
  Register #(.width(32)) register_29 (.D(col), .en(_8), .Q(ex8), .clk(clck));  // open: clr
  Register #(.width(32)) register_30 (.D(col), .en(_16), .Q(ex16), .clk(clck));  // open: clr
  Register #(.width(32)) register_31 (.D(col), .en(_24), .Q(ex24), .clk(clck));  // open: clr
  Register #(.width(32)) register_32 (.D(col), .en(_32), .Q(ex32), .clk(clck));  // open: clr

  // Other names for the same wires on the sheet: I_Oadr[3:0] = addr[3:0]; col1[31:0] = out_3; col2[31:0] = out_4;
  //   col3[31:0] = out_5; col4[31:0] = out_6; col5[31:0] = out_7; col6[31:0] = out_8; col7[31:0] = out_9;
  //   col8[31:0] = out_10; col9[31:0] = out_11; col10[31:0] = out_12; col11[31:0] = out_13; col12[31:0] = out_14;
  //   col13[31:0] = out_15; col14[31:0] = out_16; col15[31:0] = out_17; col16[31:0] = out_18; col17[31:0] = out_19;
  //   col18[31:0] = out_20; col19[31:0] = out_21; col20[31:0] = out_22; col21[31:0] = out_23; col22[31:0] = out_24;
  //   col23[31:0] = out_25; col24[31:0] = out_26; col25[31:0] = out_27; col26[31:0] = out_28; col27[31:0] = out_29;
  //   col28[31:0] = out_30; col29[31:0] = out_31; col30[31:0] = out_32; col31[31:0] = out_33; col32[31:0] = out_34;
  //   rd_wr_prime = In_Out_prime

  // Notes on the sheet:
  //   Joystick's coordinates
  //   Character's coordinates
  //   X - coordinate
  //   Y - coordinate
  //   Location controller
  //   This circuit choses location by "Number of location"
  //   Take surrounding of the character
  //   c0
  //   c8
  //   c16
  //   c24
  //   c1
  //   c9
  //   c17
  //   c25
  //   c2
  //   c10
  //   c18
  //   c26
  //   c3
  //   c11
  //   c19
  //   c27
  //   Registers for mapping on display
  //   Central Processing Unit
  //   c4
  //   c12
  //   c20
  //   c28
  //   c5
  //   c13
  //   c21
  //   c29
  //   contents of rom_1 (hex, n*v repeats v):
  //   d0 f3 b0 d1 1 34 0 e1 17 d0 f2 d1 fc b5 a1 d0 f3 d1 fd b5 a1 ee cb d0 f2 b0 d1 f0 b5 d2 2 36 a e1 2b
  //   d2 f6 ba d3 fa bf ee 63 d2 1 36 a e1 4b d1 f4 b5 5 e1 43 88 d1 f2 a4 d2 f5 ba d3 fb bf ee 49 d2 f6
  //   ba d3 fa bf ee 63 d1 f8 b5 5 e1 5d 8c d1 f2 a4 d2 f7 ba d3 f9 bf ee 63 d2 f6 ba d3 fa bf a e1 96 f
  //   e1 88 d0 a b0 0 ed 7f d0 a b0 88 d1 a a4 d0 f3 b0 8c d1 f3 a4 ee 86 d0 f3 b0 88 d1 f3 a4 ee 94 d0 a
  //   d1 0 a1 d0 f3 b0 88 d1 f3 a4 ee cb f e1 c6 d0 a b0 0 ed af d0 a b0 88 d1 a a4 d0 f3 b0 8c d1 f3 a4
  //   ee c4 d0 f1 b0 d1 1 31 5 e1 c4 d0 f3 b0 8c d1 f3 a4 d0 2 d1 a a4 ee cb d0 a d1 0 a1 d4
  //   c6
  //   c14
  //   c22
  //   c30
  //   c7
  //   c15
  //   c23
  //   c31
endmodule

// shift
module N_shift_of_1 (
  input  [4:0] N,
  output [31:0] \output 
);

  Multiplexer #(.select(5), .width(32), .enable("false")) multiplexer_1 (
    .in0(32'h1), .in1(32'h2), .in2(32'h4), .in3(32'h8), .in4(32'h10), .in5(32'h20), .in6(32'h40),
    .in7(32'h80), .in8(32'h100), .in9(32'h200), .in10(32'h400), .in11(32'h800), .in12(32'h1000),
    .in13(32'h2000), .in14(32'h4000), .in15(32'h8000), .in16(32'h10000), .in17(32'h20000), .in18(32'h40000),
    .in19(32'h80000), .in20(32'h100000), .in21(32'h200000), .in22(32'h400000), .in23(32'h800000),
    .in24(32'h1000000), .in25(32'h2000000), .in26(32'h4000000), .in27(32'h8000000), .in28(32'h10000000),
    .in29(32'h20000000), .in30(32'h40000000), .in31(32'h80000000), .out(\output ), .sel(N));
  // Probe on N
endmodule

module firstLocation (
  input  Clock,
  input  On_Off,
  output [31:0] Column,
  output [4:0] Number_of_column,
  output [4:0] X___finishTo,
  output [4:0] Y___finishTo,
  output [4:0] X___finishFrom,
  output [4:0] Y___finishFrom,
  output [4:0] X___start,
  output [4:0] Y___start
);

  wire controlled_buffer_1_out, controlled_buffer_2_out, counter_1_carry, not_1_out, not_2_out;
  wire [4:0] counter_2_q;
  wire [31:0] firstlocationdata_1_out_1, firstlocationdata_1_out_2, firstlocationdata_1_out_3,
       firstlocationdata_1_out_4, firstlocationdata_1_out_5, firstlocationdata_1_out_6,
       firstlocationdata_1_out_7, firstlocationdata_1_out_8, firstlocationdata_1_out_9,
       firstlocationdata_1_out_10, firstlocationdata_1_out_11, firstlocationdata_1_out_12,
       firstlocationdata_1_out_13, firstlocationdata_1_out_14, firstlocationdata_1_out_15,
       firstlocationdata_1_out_16, firstlocationdata_1_out_17, firstlocationdata_1_out_18,
       firstlocationdata_1_out_19, firstlocationdata_1_out_20, firstlocationdata_1_out_21,
       firstlocationdata_1_out_22, firstlocationdata_1_out_23, firstlocationdata_1_out_24,
       firstlocationdata_1_out_25, firstlocationdata_1_out_26, firstlocationdata_1_out_27,
       firstlocationdata_1_out_28, firstlocationdata_1_out_29, firstlocationdata_1_out_30,
       firstlocationdata_1_out_31, firstlocationdata_1_out_32, level_installer_1_column;

  not not_1 (not_1_out, counter_1_carry);
  not not_2 (not_2_out, counter_1_carry);
  assign controlled_buffer_1_out = not_2_out ? Clock : 1'bz;  // Controlled_Buffer controlled_buffer_1
  Counter #(.width(6), .max('h3f)) counter_1 (
    .count(controlled_buffer_1_out), .carry(counter_1_carry), .clk(controlled_buffer_1_out));  // open: load, D, Q, clr
  Multiplexer #(.width(5), .enable("false")) multiplexer_1 (
    .in1(counter_2_q), .out(Number_of_column), .sel(On_Off));  // open: in0
  Counter #(.width(5), .max('h1f)) counter_2 (
    .count(controlled_buffer_2_out), .Q(counter_2_q), .clk(controlled_buffer_2_out));  // open: load, D, carry, clr
  assign controlled_buffer_2_out = not_1_out ? Clock : 1'bz;  // Controlled_Buffer controlled_buffer_2
  firstLocationData firstlocationdata_1 (
    .out_1(firstlocationdata_1_out_1), .out_2(firstlocationdata_1_out_2), .out_3(firstlocationdata_1_out_3),
    .out_4(firstlocationdata_1_out_4), .out_5(firstlocationdata_1_out_5), .out_6(firstlocationdata_1_out_6),
    .out_7(firstlocationdata_1_out_7), .out_8(firstlocationdata_1_out_8), .out_9(firstlocationdata_1_out_9),
    .out_10(firstlocationdata_1_out_10), .out_11(firstlocationdata_1_out_11),
    .out_12(firstlocationdata_1_out_12), .out_13(firstlocationdata_1_out_13),
    .out_14(firstlocationdata_1_out_14), .out_15(firstlocationdata_1_out_15),
    .out_16(firstlocationdata_1_out_16), .out_17(firstlocationdata_1_out_17),
    .out_18(firstlocationdata_1_out_18), .out_19(firstlocationdata_1_out_19),
    .out_20(firstlocationdata_1_out_20), .out_21(firstlocationdata_1_out_21),
    .out_22(firstlocationdata_1_out_22), .out_23(firstlocationdata_1_out_23),
    .out_24(firstlocationdata_1_out_24), .out_25(firstlocationdata_1_out_25),
    .out_26(firstlocationdata_1_out_26), .out_27(firstlocationdata_1_out_27),
    .out_28(firstlocationdata_1_out_28), .out_29(firstlocationdata_1_out_29),
    .out_30(firstlocationdata_1_out_30), .out_31(firstlocationdata_1_out_31),
    .out_32(firstlocationdata_1_out_32));
  Multiplexer #(.width(5), .enable("false")) multiplexer_2 (
    .in1(5'b00010), .out(X___start), .sel(On_Off));  // open: in0
  Level_Installer level_installer_1 (
    .Number_of_column(counter_2_q), .Column(level_installer_1_column), .bus_0(firstlocationdata_1_out_1),
    .bus_1(firstlocationdata_1_out_2), .bus_2(firstlocationdata_1_out_3), .bus_3(firstlocationdata_1_out_4),
    .bus_4(firstlocationdata_1_out_5), .bus_5(firstlocationdata_1_out_6), .bus_6(firstlocationdata_1_out_7),
    .bus_7(firstlocationdata_1_out_8), .bus_8(firstlocationdata_1_out_9), .bus_9(firstlocationdata_1_out_10),
    .bus_10(firstlocationdata_1_out_11), .bus_11(firstlocationdata_1_out_12),
    .bus_12(firstlocationdata_1_out_13), .bus_13(firstlocationdata_1_out_14),
    .bus_14(firstlocationdata_1_out_15), .bus_15(firstlocationdata_1_out_16),
    .bus_16(firstlocationdata_1_out_17), .bus_17(firstlocationdata_1_out_18),
    .bus_18(firstlocationdata_1_out_19), .bus_19(firstlocationdata_1_out_20),
    .bus_20(firstlocationdata_1_out_21), .bus_21(firstlocationdata_1_out_22),
    .bus_22(firstlocationdata_1_out_23), .bus_23(firstlocationdata_1_out_24),
    .bus_24(firstlocationdata_1_out_25), .bus_25(firstlocationdata_1_out_26),
    .bus_26(firstlocationdata_1_out_27), .bus_27(firstlocationdata_1_out_28),
    .bus_28(firstlocationdata_1_out_29), .bus_29(firstlocationdata_1_out_30),
    .bus_30(firstlocationdata_1_out_31), .bus_31(firstlocationdata_1_out_32));
  Multiplexer #(.width(32), .enable("false")) multiplexer_3 (
    .in1(level_installer_1_column), .out(Column), .sel(On_Off));  // open: in0
  Multiplexer #(.width(5), .enable("false")) multiplexer_4 (
    .in1(5'b01011), .out(Y___start), .sel(On_Off));  // open: in0
  Multiplexer #(.width(5), .enable("false")) multiplexer_5 (
    .in1({5{1'b1}}), .out(X___finishTo), .sel(On_Off));  // open: in0
  Multiplexer #(.width(5), .enable("false")) multiplexer_6 (
    .in1(5'b11001), .out(Y___finishTo), .sel(On_Off));  // open: in0
  Multiplexer #(.width(5), .enable("false")) multiplexer_7 (
    .in1({5{1'b1}}), .out(X___finishFrom), .sel(On_Off));  // open: in0
  Multiplexer #(.width(5), .enable("false")) multiplexer_8 (
    .in1(5'b10100), .out(Y___finishFrom), .sel(On_Off));  // open: in0

  // Other names for the same wires on the sheet: do = On_Off

  // Notes on the sheet:
  //   Level Loader
endmodule

// Bit
module Take_N_bit (
  input  [31:0] Input,
  input  [4:0] N,
  output bus_0
);

  Multiplexer #(.select(5), .enable("false")) multiplexer_1 (
    .in0(Input[0]), .in1(Input[1]), .in2(Input[2]), .in3(Input[3]), .in4(Input[4]), .in5(Input[5]),
    .in6(Input[6]), .in7(Input[7]), .in8(Input[8]), .in9(Input[9]), .in10(Input[10]), .in11(Input[11]),
    .in12(Input[12]), .in13(Input[13]), .in14(Input[14]), .in15(Input[15]), .in16(Input[16]),
    .in17(Input[17]), .in18(Input[18]), .in19(Input[19]), .in20(Input[20]), .in21(Input[21]),
    .in22(Input[22]), .in23(Input[23]), .in24(Input[24]), .in25(Input[25]), .in26(Input[26]),
    .in27(Input[27]), .in28(Input[28]), .in29(Input[29]), .in30(Input[30]), .in31(Input[31]), .out(bus_0),
    .sel(N));
endmodule

module Win_or_not (
  input  [4:0] X___winFrom,
  input  [4:0] Y___winFrom,
  input  [4:0] X___winTo,
  input  [4:0] Y___winTo,
  input  [4:0] X,
  input  [4:0] Y,
  output _1___win_0___not
);

  wire comparator_1_eq, comparator_1_lt, comparator_2_eq, comparator_2_gt, comparator_3_eq, comparator_3_lt,
       comparator_4_eq, comparator_4_gt, or_1_out, or_2_out, or_3_out, or_4_out;

  Comparator #(.width(5), .mode("unsigned")) comparator_1 (
    .a(X___winFrom), .b(X), .eq(comparator_1_eq), .lt(comparator_1_lt));  // open: gt
  Comparator #(.width(5), .mode("unsigned")) comparator_2 (
    .a(X___winTo), .b(X), .gt(comparator_2_gt), .eq(comparator_2_eq));  // open: lt
  Comparator #(.width(5), .mode("unsigned")) comparator_3 (
    .a(Y___winFrom), .b(Y), .eq(comparator_3_eq), .lt(comparator_3_lt));  // open: gt
  Comparator #(.width(5), .mode("unsigned")) comparator_4 (
    .a(Y___winTo), .b(Y), .gt(comparator_4_gt), .eq(comparator_4_eq));  // open: lt
  or or_1 (or_1_out, comparator_1_eq, comparator_1_lt);
  or or_2 (or_2_out, comparator_2_gt, comparator_2_eq);
  or or_3 (or_3_out, comparator_3_eq, comparator_3_lt);
  or or_4 (or_4_out, comparator_4_gt, comparator_4_eq);
  and and_1 (_1___win_0___not, or_1_out, or_2_out, or_3_out, or_4_out);
endmodule

module greetingScreen (
  input  Clock,
  input  On_Off,
  output [4:0] Number_of_column,
  output [31:0] Column,
  output [4:0] X___finishTo,
  output [4:0] Y___finishTo,
  output [4:0] X___finishFrom,
  output [4:0] Y___finishFrom,
  output [4:0] X___start,
  output [4:0] Y___start
);

  wire controlled_buffer_1_out, controlled_buffer_2_out, counter_1_carry, not_1_out, not_2_out;
  wire [4:0] counter_2_q;
  wire [31:0] greetingslocftiondata_1_out_1, greetingslocftiondata_1_out_2, greetingslocftiondata_1_out_3,
       greetingslocftiondata_1_out_4, greetingslocftiondata_1_out_5, greetingslocftiondata_1_out_6,
       greetingslocftiondata_1_out_7, greetingslocftiondata_1_out_8, greetingslocftiondata_1_out_9,
       greetingslocftiondata_1_out_10, greetingslocftiondata_1_out_11, greetingslocftiondata_1_out_12,
       greetingslocftiondata_1_out_13, greetingslocftiondata_1_out_14, greetingslocftiondata_1_out_15,
       greetingslocftiondata_1_out_16, greetingslocftiondata_1_out_17, greetingslocftiondata_1_out_18,
       greetingslocftiondata_1_out_19, greetingslocftiondata_1_out_20, greetingslocftiondata_1_out_21,
       greetingslocftiondata_1_out_22, greetingslocftiondata_1_out_23, greetingslocftiondata_1_out_24,
       greetingslocftiondata_1_out_25, greetingslocftiondata_1_out_26, greetingslocftiondata_1_out_27,
       greetingslocftiondata_1_out_28, greetingslocftiondata_1_out_29, greetingslocftiondata_1_out_30,
       greetingslocftiondata_1_out_31, greetingslocftiondata_1_out_32, level_installer_1_column;

  not not_1 (not_1_out, counter_1_carry);
  not not_2 (not_2_out, counter_1_carry);
  assign controlled_buffer_1_out = not_2_out ? Clock : 1'bz;  // Controlled_Buffer controlled_buffer_1
  Counter #(.width(6), .max('h3f)) counter_1 (
    .count(controlled_buffer_1_out), .carry(counter_1_carry), .clk(controlled_buffer_1_out));  // open: load, D, Q, clr
  Multiplexer #(.width(5), .enable("false")) multiplexer_1 (
    .in1(counter_2_q), .out(Number_of_column), .sel(On_Off));  // open: in0
  Counter #(.width(5), .max('h1f)) counter_2 (
    .count(controlled_buffer_2_out), .Q(counter_2_q), .clk(controlled_buffer_2_out));  // open: load, D, carry, clr
  assign controlled_buffer_2_out = not_1_out ? Clock : 1'bz;  // Controlled_Buffer controlled_buffer_2
  greetingsLocftionData greetingslocftiondata_1 (
    .out_1(greetingslocftiondata_1_out_1), .out_2(greetingslocftiondata_1_out_2),
    .out_3(greetingslocftiondata_1_out_3), .out_4(greetingslocftiondata_1_out_4),
    .out_5(greetingslocftiondata_1_out_5), .out_6(greetingslocftiondata_1_out_6),
    .out_7(greetingslocftiondata_1_out_7), .out_8(greetingslocftiondata_1_out_8),
    .out_9(greetingslocftiondata_1_out_9), .out_10(greetingslocftiondata_1_out_10),
    .out_11(greetingslocftiondata_1_out_11), .out_12(greetingslocftiondata_1_out_12),
    .out_13(greetingslocftiondata_1_out_13), .out_14(greetingslocftiondata_1_out_14),
    .out_15(greetingslocftiondata_1_out_15), .out_16(greetingslocftiondata_1_out_16),
    .out_17(greetingslocftiondata_1_out_17), .out_18(greetingslocftiondata_1_out_18),
    .out_19(greetingslocftiondata_1_out_19), .out_20(greetingslocftiondata_1_out_20),
    .out_21(greetingslocftiondata_1_out_21), .out_22(greetingslocftiondata_1_out_22),
    .out_23(greetingslocftiondata_1_out_23), .out_24(greetingslocftiondata_1_out_24),
    .out_25(greetingslocftiondata_1_out_25), .out_26(greetingslocftiondata_1_out_26),
    .out_27(greetingslocftiondata_1_out_27), .out_28(greetingslocftiondata_1_out_28),
    .out_29(greetingslocftiondata_1_out_29), .out_30(greetingslocftiondata_1_out_30),
    .out_31(greetingslocftiondata_1_out_31), .out_32(greetingslocftiondata_1_out_32));
  Multiplexer #(.width(5), .enable("false")) multiplexer_2 (
    .in1(5'b10100), .out(X___start), .sel(On_Off));  // open: in0
  Level_Installer level_installer_1 (
    .Number_of_column(counter_2_q), .Column(level_installer_1_column), .bus_0(greetingslocftiondata_1_out_1),
    .bus_1(greetingslocftiondata_1_out_2), .bus_2(greetingslocftiondata_1_out_3),
    .bus_3(greetingslocftiondata_1_out_4), .bus_4(greetingslocftiondata_1_out_5),
    .bus_5(greetingslocftiondata_1_out_6), .bus_6(greetingslocftiondata_1_out_7),
    .bus_7(greetingslocftiondata_1_out_8), .bus_8(greetingslocftiondata_1_out_9),
    .bus_9(greetingslocftiondata_1_out_10), .bus_10(greetingslocftiondata_1_out_11),
    .bus_11(greetingslocftiondata_1_out_12), .bus_12(greetingslocftiondata_1_out_13),
    .bus_13(greetingslocftiondata_1_out_14), .bus_14(greetingslocftiondata_1_out_15),
    .bus_15(greetingslocftiondata_1_out_16), .bus_16(greetingslocftiondata_1_out_17),
    .bus_17(greetingslocftiondata_1_out_18), .bus_18(greetingslocftiondata_1_out_19),
    .bus_19(greetingslocftiondata_1_out_20), .bus_20(greetingslocftiondata_1_out_21),
    .bus_21(greetingslocftiondata_1_out_22), .bus_22(greetingslocftiondata_1_out_23),
    .bus_23(greetingslocftiondata_1_out_24), .bus_24(greetingslocftiondata_1_out_25),
    .bus_25(greetingslocftiondata_1_out_26), .bus_26(greetingslocftiondata_1_out_27),
    .bus_27(greetingslocftiondata_1_out_28), .bus_28(greetingslocftiondata_1_out_29),
    .bus_29(greetingslocftiondata_1_out_30), .bus_30(greetingslocftiondata_1_out_31),
    .bus_31(greetingslocftiondata_1_out_32));
  Multiplexer #(.width(32), .enable("false")) multiplexer_3 (
    .in1(level_installer_1_column), .out(Column), .sel(On_Off));  // open: in0
  Multiplexer #(.width(5), .enable("false")) multiplexer_4 (
    .in1(5'b01000), .out(Y___start), .sel(On_Off));  // open: in0
  Multiplexer #(.width(5), .enable("false")) multiplexer_5 (
    .in1({5{1'b1}}), .out(X___finishTo), .sel(On_Off));  // open: in0
  Multiplexer #(.width(5), .enable("false")) multiplexer_6 (
    .in1(5'b10000), .out(Y___finishTo), .sel(On_Off));  // open: in0
  Multiplexer #(.width(5), .enable("false")) multiplexer_7 (
    .in1(5'b11110), .out(X___finishFrom), .sel(On_Off));  // open: in0
  Multiplexer #(.width(5), .enable("false")) multiplexer_8 (
    .in1(5'b01010), .out(Y___finishFrom), .sel(On_Off));  // open: in0

  // Other names for the same wires on the sheet: do = On_Off

  // Notes on the sheet:
  //   Location Loader
endmodule

module greetingsLocftionData (
  output [31:0] out_1,
  output [31:0] out_2,
  output [31:0] out_3,
  output [31:0] out_4,
  output [31:0] out_5,
  output [31:0] out_6,
  output [31:0] out_7,
  output [31:0] out_8,
  output [31:0] out_9,
  output [31:0] out_10,
  output [31:0] out_11,
  output [31:0] out_12,
  output [31:0] out_13,
  output [31:0] out_14,
  output [31:0] out_15,
  output [31:0] out_16,
  output [31:0] out_17,
  output [31:0] out_18,
  output [31:0] out_19,
  output [31:0] out_20,
  output [31:0] out_21,
  output [31:0] out_22,
  output [31:0] out_23,
  output [31:0] out_24,
  output [31:0] out_25,
  output [31:0] out_26,
  output [31:0] out_27,
  output [31:0] out_28,
  output [31:0] out_29,
  output [31:0] out_30,
  output [31:0] out_31,
  output [31:0] out_32
);


  assign out_1 = 32'hff800;
  assign out_2 = 32'h7c000800;
  assign out_3 = 32'h5003a800;
  assign out_4 = 32'h7002e800;
  assign out_5 = 32'h800;
  assign out_6 = 32'h7c03c800;
  assign out_7 = 32'ha800;
  assign out_8 = 32'h1c000800;
  assign out_9 = 32'h2800e800;
  assign out_10 = 32'h1c014800;
  assign out_11 = 32'he800;
  assign out_12 = 32'h78000800;
  assign out_13 = 32'h1400e800;
  assign out_14 = 32'h8fe0;
  assign out_15 = 32'h3c004820;
  assign out_16 = 32'h50000820;
  assign out_17 = 32'h3c820;
  assign out_18 = 32'h1c00a820;
  assign out_19 = 32'h14000820;
  assign out_20 = 32'h1c000b20;
  assign out_21 = 32'ha20;
  assign out_22 = 32'h1c000b20;
  assign out_23 = 32'h10000020;
  assign out_24 = 32'h8008020;
  assign out_25 = 32'h8040;
  assign out_26 = 32'h1c02a080;
  assign out_27 = 32'h1001c100;
  assign out_28 = 32'h8008200;
  assign out_29 = 32'h10000400;
  assign out_30 = 32'h1c000800;
  assign out_31 = 32'h800;
  assign out_32 = 32'h800;
endmodule

module firstLocationData (
  output [31:0] out_1,
  output [31:0] out_2,
  output [31:0] out_3,
  output [31:0] out_4,
  output [31:0] out_5,
  output [31:0] out_6,
  output [31:0] out_7,
  output [31:0] out_8,
  output [31:0] out_9,
  output [31:0] out_10,
  output [31:0] out_11,
  output [31:0] out_12,
  output [31:0] out_13,
  output [31:0] out_14,
  output [31:0] out_15,
  output [31:0] out_16,
  output [31:0] out_17,
  output [31:0] out_18,
  output [31:0] out_19,
  output [31:0] out_20,
  output [31:0] out_21,
  output [31:0] out_22,
  output [31:0] out_23,
  output [31:0] out_24,
  output [31:0] out_25,
  output [31:0] out_26,
  output [31:0] out_27,
  output [31:0] out_28,
  output [31:0] out_29,
  output [31:0] out_30,
  output [31:0] out_31,
  output [31:0] out_32
);


  assign out_1 = 32'hffff81ff;
  assign out_2 = 32'h80000101;
  assign out_3 = 32'h80000101;
  assign out_4 = 32'h80000101;
  assign out_5 = 32'h80000101;
  assign out_6 = 32'h80000001;
  assign out_7 = 32'h80000001;
  assign out_8 = 32'h80000401;
  assign out_9 = 32'h80000401;
  assign out_10 = 32'h80000001;
  assign out_11 = 32'h80000001;
  assign out_12 = 32'h80000001;
  assign out_13 = 32'h80000001;
  assign out_14 = 32'h80000401;
  assign out_15 = 32'h80000401;
  assign out_16 = 32'h80000001;
  assign out_17 = 32'h80000001;
  assign out_18 = 32'h80000001;
  assign out_19 = 32'h80000001;
  assign out_20 = 32'h80000201;
  assign out_21 = 32'h80000201;
  assign out_22 = 32'h80000001;
  assign out_23 = 32'h80000001;
  assign out_24 = 32'h80000001;
  assign out_25 = 32'h80000401;
  assign out_26 = 32'h80000401;
  assign out_27 = 32'h80000001;
  assign out_28 = 32'h80001001;
  assign out_29 = 32'h80009001;
  assign out_30 = 32'h80049001;
  assign out_31 = 32'h80049001;
  assign out_32 = 32'hfc0fffff;
endmodule

module secondLocation (
  input  Clock,
  input  On_Off,
  output [31:0] Column,
  output [4:0] Number_of_column,
  output [4:0] X___finishTo,
  output [4:0] Y___finishTo,
  output [4:0] X___finishFrom,
  output [4:0] Y___finishFrom,
  output [4:0] X___start,
  output [4:0] Y___start
);

  wire controlled_buffer_1_out, controlled_buffer_2_out, counter_1_carry, not_1_out, not_2_out;
  wire [4:0] counter_2_q;
  wire [31:0] level_installer_1_column, secondlocationdata_1_out_1, secondlocationdata_1_out_2,
       secondlocationdata_1_out_3, secondlocationdata_1_out_4, secondlocationdata_1_out_5,
       secondlocationdata_1_out_6, secondlocationdata_1_out_7, secondlocationdata_1_out_8,
       secondlocationdata_1_out_9, secondlocationdata_1_out_10, secondlocationdata_1_out_11,
       secondlocationdata_1_out_12, secondlocationdata_1_out_13, secondlocationdata_1_out_14,
       secondlocationdata_1_out_15, secondlocationdata_1_out_16, secondlocationdata_1_out_17,
       secondlocationdata_1_out_18, secondlocationdata_1_out_19, secondlocationdata_1_out_20,
       secondlocationdata_1_out_21, secondlocationdata_1_out_22, secondlocationdata_1_out_23,
       secondlocationdata_1_out_24, secondlocationdata_1_out_25, secondlocationdata_1_out_26,
       secondlocationdata_1_out_27, secondlocationdata_1_out_28, secondlocationdata_1_out_29,
       secondlocationdata_1_out_30, secondlocationdata_1_out_31, secondlocationdata_1_out_32;

  not not_1 (not_1_out, counter_1_carry);
  not not_2 (not_2_out, counter_1_carry);
  assign controlled_buffer_1_out = not_2_out ? Clock : 1'bz;  // Controlled_Buffer controlled_buffer_1
  Counter #(.width(6), .max('h3f)) counter_1 (
    .count(controlled_buffer_1_out), .carry(counter_1_carry), .clk(controlled_buffer_1_out));  // open: load, D, Q, clr
  Multiplexer #(.width(5), .enable("false")) multiplexer_1 (
    .in1(counter_2_q), .out(Number_of_column), .sel(On_Off));  // open: in0
  Counter #(.width(5), .max('h1f)) counter_2 (
    .count(controlled_buffer_2_out), .Q(counter_2_q), .clk(controlled_buffer_2_out));  // open: load, D, carry, clr
  assign controlled_buffer_2_out = not_1_out ? Clock : 1'bz;  // Controlled_Buffer controlled_buffer_2
  secondLocationData secondlocationdata_1 (
    .out_1(secondlocationdata_1_out_1), .out_2(secondlocationdata_1_out_2),
    .out_3(secondlocationdata_1_out_3), .out_4(secondlocationdata_1_out_4),
    .out_5(secondlocationdata_1_out_5), .out_6(secondlocationdata_1_out_6),
    .out_7(secondlocationdata_1_out_7), .out_8(secondlocationdata_1_out_8),
    .out_9(secondlocationdata_1_out_9), .out_10(secondlocationdata_1_out_10),
    .out_11(secondlocationdata_1_out_11), .out_12(secondlocationdata_1_out_12),
    .out_13(secondlocationdata_1_out_13), .out_14(secondlocationdata_1_out_14),
    .out_15(secondlocationdata_1_out_15), .out_16(secondlocationdata_1_out_16),
    .out_17(secondlocationdata_1_out_17), .out_18(secondlocationdata_1_out_18),
    .out_19(secondlocationdata_1_out_19), .out_20(secondlocationdata_1_out_20),
    .out_21(secondlocationdata_1_out_21), .out_22(secondlocationdata_1_out_22),
    .out_23(secondlocationdata_1_out_23), .out_24(secondlocationdata_1_out_24),
    .out_25(secondlocationdata_1_out_25), .out_26(secondlocationdata_1_out_26),
    .out_27(secondlocationdata_1_out_27), .out_28(secondlocationdata_1_out_28),
    .out_29(secondlocationdata_1_out_29), .out_30(secondlocationdata_1_out_30),
    .out_31(secondlocationdata_1_out_31), .out_32(secondlocationdata_1_out_32));
  Multiplexer #(.width(5), .enable("false")) multiplexer_2 (
    .in1(5'b00010), .out(X___start), .sel(On_Off));  // open: in0
  Level_Installer level_installer_1 (
    .Number_of_column(counter_2_q), .Column(level_installer_1_column), .bus_0(secondlocationdata_1_out_1),
    .bus_1(secondlocationdata_1_out_2), .bus_2(secondlocationdata_1_out_3),
    .bus_3(secondlocationdata_1_out_4), .bus_4(secondlocationdata_1_out_5),
    .bus_5(secondlocationdata_1_out_6), .bus_6(secondlocationdata_1_out_7),
    .bus_7(secondlocationdata_1_out_8), .bus_8(secondlocationdata_1_out_9),
    .bus_9(secondlocationdata_1_out_10), .bus_10(secondlocationdata_1_out_11),
    .bus_11(secondlocationdata_1_out_12), .bus_12(secondlocationdata_1_out_13),
    .bus_13(secondlocationdata_1_out_14), .bus_14(secondlocationdata_1_out_15),
    .bus_15(secondlocationdata_1_out_16), .bus_16(secondlocationdata_1_out_17),
    .bus_17(secondlocationdata_1_out_18), .bus_18(secondlocationdata_1_out_19),
    .bus_19(secondlocationdata_1_out_20), .bus_20(secondlocationdata_1_out_21),
    .bus_21(secondlocationdata_1_out_22), .bus_22(secondlocationdata_1_out_23),
    .bus_23(secondlocationdata_1_out_24), .bus_24(secondlocationdata_1_out_25),
    .bus_25(secondlocationdata_1_out_26), .bus_26(secondlocationdata_1_out_27),
    .bus_27(secondlocationdata_1_out_28), .bus_28(secondlocationdata_1_out_29),
    .bus_29(secondlocationdata_1_out_30), .bus_30(secondlocationdata_1_out_31),
    .bus_31(secondlocationdata_1_out_32));
  Multiplexer #(.width(32), .enable("false")) multiplexer_3 (
    .in1(level_installer_1_column), .out(Column), .sel(On_Off));  // open: in0
  Multiplexer #(.width(5), .enable("false")) multiplexer_4 (
    .in1(5'b00111), .out(Y___start), .sel(On_Off));  // open: in0
  Multiplexer #(.width(5), .enable("false")) multiplexer_5 (
    .in1({5{1'b1}}), .out(X___finishTo), .sel(On_Off));  // open: in0
  Multiplexer #(.width(5), .enable("false")) multiplexer_6 (
    .in1(5'b01000), .out(Y___finishTo), .sel(On_Off));  // open: in0
  Multiplexer #(.width(5), .enable("false")) multiplexer_7 (
    .in1({5{1'b1}}), .out(X___finishFrom), .sel(On_Off));  // open: in0
  Multiplexer #(.width(5), .enable("false")) multiplexer_8 (
    .in1(5'b00011), .out(Y___finishFrom), .sel(On_Off));  // open: in0

  // Other names for the same wires on the sheet: do = On_Off

  // Notes on the sheet:
  //   Level Loader
endmodule

module secondLocationData (
  output [31:0] out_1,
  output [31:0] out_2,
  output [31:0] out_3,
  output [31:0] out_4,
  output [31:0] out_5,
  output [31:0] out_6,
  output [31:0] out_7,
  output [31:0] out_8,
  output [31:0] out_9,
  output [31:0] out_10,
  output [31:0] out_11,
  output [31:0] out_12,
  output [31:0] out_13,
  output [31:0] out_14,
  output [31:0] out_15,
  output [31:0] out_16,
  output [31:0] out_17,
  output [31:0] out_18,
  output [31:0] out_19,
  output [31:0] out_20,
  output [31:0] out_21,
  output [31:0] out_22,
  output [31:0] out_23,
  output [31:0] out_24,
  output [31:0] out_25,
  output [31:0] out_26,
  output [31:0] out_27,
  output [31:0] out_28,
  output [31:0] out_29,
  output [31:0] out_30,
  output [31:0] out_31,
  output [31:0] out_32
);


  assign out_1 = 32'hfffffc0f;
  assign out_2 = 32'h80000009;
  assign out_3 = 32'h80000009;
  assign out_4 = 32'h80000009;
  assign out_5 = 32'h80000001;
  assign out_6 = 32'h80000021;
  assign out_7 = 32'h80000021;
  assign out_8 = 32'h80000001;
  assign out_9 = 32'h80000081;
  assign out_10 = 32'h80000081;
  assign out_11 = 32'h80000001;
  assign out_12 = 32'h80000201;
  assign out_13 = 32'h80000201;
  assign out_14 = 32'h80000001;
  assign out_15 = 32'h80000801;
  assign out_16 = 32'h80000801;
  assign out_17 = 32'h80000001;
  assign out_18 = 32'h80000001;
  assign out_19 = 32'h80000001;
  assign out_20 = 32'h80000001;
  assign out_21 = 32'h80000001;
  assign out_22 = 32'h80000001;
  assign out_23 = 32'h80000001;
  assign out_24 = 32'h80000001;
  assign out_25 = 32'h80000001;
  assign out_26 = 32'h80000001;
  assign out_27 = 32'h80000001;
  assign out_28 = 32'h80000001;
  assign out_29 = 32'h80000001;
  assign out_30 = 32'h80000005;
  assign out_31 = 32'h80000005;
  assign out_32 = 32'hfffffe07;
endmodule

module thirdLocation (
  input  Clock,
  input  On_Off,
  output [31:0] Column,
  output [4:0] Number_of_column,
  output [4:0] X___finishTo,
  output [4:0] Y___finishTo,
  output [4:0] X___finishFrom,
  output [4:0] Y___finishFrom,
  output [4:0] X___start,
  output [4:0] Y___start
);

  wire controlled_buffer_1_out, controlled_buffer_2_out, counter_1_carry, not_1_out, not_2_out;
  wire [4:0] counter_2_q;
  wire [31:0] level_installer_1_column, thirdlocationdata_1_out_1, thirdlocationdata_1_out_2,
       thirdlocationdata_1_out_3, thirdlocationdata_1_out_4, thirdlocationdata_1_out_5,
       thirdlocationdata_1_out_6, thirdlocationdata_1_out_7, thirdlocationdata_1_out_8,
       thirdlocationdata_1_out_9, thirdlocationdata_1_out_10, thirdlocationdata_1_out_11,
       thirdlocationdata_1_out_12, thirdlocationdata_1_out_13, thirdlocationdata_1_out_14,
       thirdlocationdata_1_out_15, thirdlocationdata_1_out_16, thirdlocationdata_1_out_17,
       thirdlocationdata_1_out_18, thirdlocationdata_1_out_19, thirdlocationdata_1_out_20,
       thirdlocationdata_1_out_21, thirdlocationdata_1_out_22, thirdlocationdata_1_out_23,
       thirdlocationdata_1_out_24, thirdlocationdata_1_out_25, thirdlocationdata_1_out_26,
       thirdlocationdata_1_out_27, thirdlocationdata_1_out_28, thirdlocationdata_1_out_29,
       thirdlocationdata_1_out_30, thirdlocationdata_1_out_31, thirdlocationdata_1_out_32;

  not not_1 (not_1_out, counter_1_carry);
  not not_2 (not_2_out, counter_1_carry);
  assign controlled_buffer_1_out = not_2_out ? Clock : 1'bz;  // Controlled_Buffer controlled_buffer_1
  Counter #(.width(6), .max('h3f)) counter_1 (
    .count(controlled_buffer_1_out), .carry(counter_1_carry), .clk(controlled_buffer_1_out));  // open: load, D, Q, clr
  Multiplexer #(.width(5), .enable("false")) multiplexer_1 (
    .in1(counter_2_q), .out(Number_of_column), .sel(On_Off));  // open: in0
  Counter #(.width(5), .max('h1f)) counter_2 (
    .count(controlled_buffer_2_out), .Q(counter_2_q), .clk(controlled_buffer_2_out));  // open: load, D, carry, clr
  assign controlled_buffer_2_out = not_1_out ? Clock : 1'bz;  // Controlled_Buffer controlled_buffer_2
  thirdLocationData thirdlocationdata_1 (
    .out_1(thirdlocationdata_1_out_1), .out_2(thirdlocationdata_1_out_2), .out_3(thirdlocationdata_1_out_3),
    .out_4(thirdlocationdata_1_out_4), .out_5(thirdlocationdata_1_out_5), .out_6(thirdlocationdata_1_out_6),
    .out_7(thirdlocationdata_1_out_7), .out_8(thirdlocationdata_1_out_8), .out_9(thirdlocationdata_1_out_9),
    .out_10(thirdlocationdata_1_out_10), .out_11(thirdlocationdata_1_out_11),
    .out_12(thirdlocationdata_1_out_12), .out_13(thirdlocationdata_1_out_13),
    .out_14(thirdlocationdata_1_out_14), .out_15(thirdlocationdata_1_out_15),
    .out_16(thirdlocationdata_1_out_16), .out_17(thirdlocationdata_1_out_17),
    .out_18(thirdlocationdata_1_out_18), .out_19(thirdlocationdata_1_out_19),
    .out_20(thirdlocationdata_1_out_20), .out_21(thirdlocationdata_1_out_21),
    .out_22(thirdlocationdata_1_out_22), .out_23(thirdlocationdata_1_out_23),
    .out_24(thirdlocationdata_1_out_24), .out_25(thirdlocationdata_1_out_25),
    .out_26(thirdlocationdata_1_out_26), .out_27(thirdlocationdata_1_out_27),
    .out_28(thirdlocationdata_1_out_28), .out_29(thirdlocationdata_1_out_29),
    .out_30(thirdlocationdata_1_out_30), .out_31(thirdlocationdata_1_out_31),
    .out_32(thirdlocationdata_1_out_32));
  Multiplexer #(.width(5), .enable("false")) multiplexer_2 (
    .in1(5'b00010), .out(X___start), .sel(On_Off));  // open: in0
  Level_Installer level_installer_1 (
    .Number_of_column(counter_2_q), .Column(level_installer_1_column), .bus_0(thirdlocationdata_1_out_1),
    .bus_1(thirdlocationdata_1_out_2), .bus_2(thirdlocationdata_1_out_3), .bus_3(thirdlocationdata_1_out_4),
    .bus_4(thirdlocationdata_1_out_5), .bus_5(thirdlocationdata_1_out_6), .bus_6(thirdlocationdata_1_out_7),
    .bus_7(thirdlocationdata_1_out_8), .bus_8(thirdlocationdata_1_out_9), .bus_9(thirdlocationdata_1_out_10),
    .bus_10(thirdlocationdata_1_out_11), .bus_11(thirdlocationdata_1_out_12),
    .bus_12(thirdlocationdata_1_out_13), .bus_13(thirdlocationdata_1_out_14),
    .bus_14(thirdlocationdata_1_out_15), .bus_15(thirdlocationdata_1_out_16),
    .bus_16(thirdlocationdata_1_out_17), .bus_17(thirdlocationdata_1_out_18),
    .bus_18(thirdlocationdata_1_out_19), .bus_19(thirdlocationdata_1_out_20),
    .bus_20(thirdlocationdata_1_out_21), .bus_21(thirdlocationdata_1_out_22),
    .bus_22(thirdlocationdata_1_out_23), .bus_23(thirdlocationdata_1_out_24),
    .bus_24(thirdlocationdata_1_out_25), .bus_25(thirdlocationdata_1_out_26),
    .bus_26(thirdlocationdata_1_out_27), .bus_27(thirdlocationdata_1_out_28),
    .bus_28(thirdlocationdata_1_out_29), .bus_29(thirdlocationdata_1_out_30),
    .bus_30(thirdlocationdata_1_out_31), .bus_31(thirdlocationdata_1_out_32));
  Multiplexer #(.width(32), .enable("false")) multiplexer_3 (
    .in1(level_installer_1_column), .out(Column), .sel(On_Off));  // open: in0
  Multiplexer #(.width(5), .enable("false")) multiplexer_4 (
    .in1(5'b00110), .out(Y___start), .sel(On_Off));  // open: in0
  Multiplexer #(.width(5), .enable("false")) multiplexer_5 (
    .in1(5'b10010), .out(X___finishTo), .sel(On_Off));  // open: in0
  Multiplexer #(.width(5), .enable("false")) multiplexer_6 (
    .in1({5{1'b1}}), .out(Y___finishTo), .sel(On_Off));  // open: in0
  Multiplexer #(.width(5), .enable("false")) multiplexer_7 (
    .in1(5'b01101), .out(X___finishFrom), .sel(On_Off));  // open: in0
  Multiplexer #(.width(5), .enable("false")) multiplexer_8 (
    .in1({5{1'b1}}), .out(Y___finishFrom), .sel(On_Off));  // open: in0

  // Other names for the same wires on the sheet: do = On_Off

  // Notes on the sheet:
  //   Level Loader
endmodule

module thirdLocationData (
  output [31:0] out_1,
  output [31:0] out_2,
  output [31:0] out_3,
  output [31:0] out_4,
  output [31:0] out_5,
  output [31:0] out_6,
  output [31:0] out_7,
  output [31:0] out_8,
  output [31:0] out_9,
  output [31:0] out_10,
  output [31:0] out_11,
  output [31:0] out_12,
  output [31:0] out_13,
  output [31:0] out_14,
  output [31:0] out_15,
  output [31:0] out_16,
  output [31:0] out_17,
  output [31:0] out_18,
  output [31:0] out_19,
  output [31:0] out_20,
  output [31:0] out_21,
  output [31:0] out_22,
  output [31:0] out_23,
  output [31:0] out_24,
  output [31:0] out_25,
  output [31:0] out_26,
  output [31:0] out_27,
  output [31:0] out_28,
  output [31:0] out_29,
  output [31:0] out_30,
  output [31:0] out_31,
  output [31:0] out_32
);


  assign out_1 = 32'hfffffc0f;
  assign out_2 = 32'h80000009;
  assign out_3 = 32'h80000009;
  assign out_4 = 32'h80000001;
  assign out_5 = 32'h80000021;
  assign out_6 = 32'h80000021;
  assign out_7 = 32'h80000081;
  assign out_8 = 32'h80000081;
  assign out_9 = 32'h80002201;
  assign out_10 = 32'h80002201;
  assign out_11 = 32'h80008801;
  assign out_12 = 32'h80008801;
  assign out_13 = 32'h80000001;
  assign out_14 = 32'h10000001;
  assign out_15 = 32'h10000001;
  assign out_16 = 32'h4000001;
  assign out_17 = 32'h4008001;
  assign out_18 = 32'h10008001;
  assign out_19 = 32'h10800001;
  assign out_20 = 32'h80820001;
  assign out_21 = 32'h80120001;
  assign out_22 = 32'h80100001;
  assign out_23 = 32'h80000001;
  assign out_24 = 32'h80000001;
  assign out_25 = 32'h80000001;
  assign out_26 = 32'h80000001;
  assign out_27 = 32'h80000001;
  assign out_28 = 32'h80000001;
  assign out_29 = 32'h80000001;
  assign out_30 = 32'h80000001;
  assign out_31 = 32'h80000001;
  assign out_32 = {32{1'b1}};
endmodule

module _4locationData (
  output [31:0] out_1,
  output [31:0] out_2,
  output [31:0] out_3,
  output [31:0] out_4,
  output [31:0] out_5,
  output [31:0] out_6,
  output [31:0] out_7,
  output [31:0] out_8,
  output [31:0] out_9,
  output [31:0] out_10,
  output [31:0] out_11,
  output [31:0] out_12,
  output [31:0] out_13,
  output [31:0] out_14,
  output [31:0] out_15,
  output [31:0] out_16,
  output [31:0] out_17,
  output [31:0] out_18,
  output [31:0] out_19,
  output [31:0] out_20,
  output [31:0] out_21,
  output [31:0] out_22,
  output [31:0] out_23,
  output [31:0] out_24,
  output [31:0] out_25,
  output [31:0] out_26,
  output [31:0] out_27,
  output [31:0] out_28,
  output [31:0] out_29,
  output [31:0] out_30,
  output [31:0] out_31,
  output [31:0] out_32
);


  assign out_1 = {32{1'b1}};
  assign out_2 = 32'h80000001;
  assign out_3 = 32'h80000001;
  assign out_4 = 32'h80000001;
  assign out_5 = 32'h80000001;
  assign out_6 = 32'h80000001;
  assign out_7 = 32'h80000021;
  assign out_8 = 32'h80000021;
  assign out_9 = 32'h80000039;
  assign out_10 = 32'h80000009;
  assign out_11 = 32'h8000000f;
  assign out_12 = 32'h80000009;
  assign out_13 = 32'h80000009;
  assign out_14 = 32'h80000009;
  assign out_15 = 32'h80000009;
  assign out_16 = 32'h80000009;
  assign out_17 = 32'h8000000f;
  assign out_18 = 32'h80000009;
  assign out_19 = 32'h80000039;
  assign out_20 = 32'h80000021;
  assign out_21 = 32'h80000021;
  assign out_22 = 32'h80000001;
  assign out_23 = 32'h80000881;
  assign out_24 = 32'h80000881;
  assign out_25 = 32'h80004201;
  assign out_26 = 32'h8000c201;
  assign out_27 = 32'h80008001;
  assign out_28 = 32'h80000001;
  assign out_29 = 32'h80000001;
  assign out_30 = 32'h80090001;
  assign out_31 = 32'h80410001;
  assign out_32 = 32'h81ffffff;
endmodule

module _4location (
  input  Clock,
  input  On_Off,
  output [31:0] Column,
  output [4:0] Number_of_column,
  output [4:0] X___finishTo,
  output [4:0] Y___finishTo,
  output [4:0] X___finishFrom,
  output [4:0] Y___finishFrom,
  output [4:0] X___start,
  output [4:0] Y___start
);

  wire controlled_buffer_1_out, controlled_buffer_2_out, counter_1_carry, not_1_out, not_2_out;
  wire [4:0] counter_2_q;
  wire [31:0] level_installer_1_column, n4locationdata_1_out_1, n4locationdata_1_out_2,
       n4locationdata_1_out_3, n4locationdata_1_out_4, n4locationdata_1_out_5, n4locationdata_1_out_6,
       n4locationdata_1_out_7, n4locationdata_1_out_8, n4locationdata_1_out_9, n4locationdata_1_out_10,
       n4locationdata_1_out_11, n4locationdata_1_out_12, n4locationdata_1_out_13, n4locationdata_1_out_14,
       n4locationdata_1_out_15, n4locationdata_1_out_16, n4locationdata_1_out_17, n4locationdata_1_out_18,
       n4locationdata_1_out_19, n4locationdata_1_out_20, n4locationdata_1_out_21, n4locationdata_1_out_22,
       n4locationdata_1_out_23, n4locationdata_1_out_24, n4locationdata_1_out_25, n4locationdata_1_out_26,
       n4locationdata_1_out_27, n4locationdata_1_out_28, n4locationdata_1_out_29, n4locationdata_1_out_30,
       n4locationdata_1_out_31, n4locationdata_1_out_32;

  not not_1 (not_1_out, counter_1_carry);
  not not_2 (not_2_out, counter_1_carry);
  assign controlled_buffer_1_out = not_2_out ? Clock : 1'bz;  // Controlled_Buffer controlled_buffer_1
  Counter #(.width(6), .max('h3f)) counter_1 (
    .count(controlled_buffer_1_out), .carry(counter_1_carry), .clk(controlled_buffer_1_out));  // open: load, D, Q, clr
  Multiplexer #(.width(5), .enable("false")) multiplexer_1 (
    .in1(counter_2_q), .out(Number_of_column), .sel(On_Off));  // open: in0
  Counter #(.width(5), .max('h1f)) counter_2 (
    .count(controlled_buffer_2_out), .Q(counter_2_q), .clk(controlled_buffer_2_out));  // open: load, D, carry, clr
  assign controlled_buffer_2_out = not_1_out ? Clock : 1'bz;  // Controlled_Buffer controlled_buffer_2
  _4locationData u_4locationdata_1 (
    .out_1(n4locationdata_1_out_1), .out_2(n4locationdata_1_out_2), .out_3(n4locationdata_1_out_3),
    .out_4(n4locationdata_1_out_4), .out_5(n4locationdata_1_out_5), .out_6(n4locationdata_1_out_6),
    .out_7(n4locationdata_1_out_7), .out_8(n4locationdata_1_out_8), .out_9(n4locationdata_1_out_9),
    .out_10(n4locationdata_1_out_10), .out_11(n4locationdata_1_out_11), .out_12(n4locationdata_1_out_12),
    .out_13(n4locationdata_1_out_13), .out_14(n4locationdata_1_out_14), .out_15(n4locationdata_1_out_15),
    .out_16(n4locationdata_1_out_16), .out_17(n4locationdata_1_out_17), .out_18(n4locationdata_1_out_18),
    .out_19(n4locationdata_1_out_19), .out_20(n4locationdata_1_out_20), .out_21(n4locationdata_1_out_21),
    .out_22(n4locationdata_1_out_22), .out_23(n4locationdata_1_out_23), .out_24(n4locationdata_1_out_24),
    .out_25(n4locationdata_1_out_25), .out_26(n4locationdata_1_out_26), .out_27(n4locationdata_1_out_27),
    .out_28(n4locationdata_1_out_28), .out_29(n4locationdata_1_out_29), .out_30(n4locationdata_1_out_30),
    .out_31(n4locationdata_1_out_31), .out_32(n4locationdata_1_out_32));
  Multiplexer #(.width(5), .enable("false")) multiplexer_2 (
    .in1(5'b01101), .out(X___start), .sel(On_Off));  // open: in0
  Level_Installer level_installer_1 (
    .Number_of_column(counter_2_q), .Column(level_installer_1_column), .bus_0(n4locationdata_1_out_1),
    .bus_1(n4locationdata_1_out_2), .bus_2(n4locationdata_1_out_3), .bus_3(n4locationdata_1_out_4),
    .bus_4(n4locationdata_1_out_5), .bus_5(n4locationdata_1_out_6), .bus_6(n4locationdata_1_out_7),
    .bus_7(n4locationdata_1_out_8), .bus_8(n4locationdata_1_out_9), .bus_9(n4locationdata_1_out_10),
    .bus_10(n4locationdata_1_out_11), .bus_11(n4locationdata_1_out_12), .bus_12(n4locationdata_1_out_13),
    .bus_13(n4locationdata_1_out_14), .bus_14(n4locationdata_1_out_15), .bus_15(n4locationdata_1_out_16),
    .bus_16(n4locationdata_1_out_17), .bus_17(n4locationdata_1_out_18), .bus_18(n4locationdata_1_out_19),
    .bus_19(n4locationdata_1_out_20), .bus_20(n4locationdata_1_out_21), .bus_21(n4locationdata_1_out_22),
    .bus_22(n4locationdata_1_out_23), .bus_23(n4locationdata_1_out_24), .bus_24(n4locationdata_1_out_25),
    .bus_25(n4locationdata_1_out_26), .bus_26(n4locationdata_1_out_27), .bus_27(n4locationdata_1_out_28),
    .bus_28(n4locationdata_1_out_29), .bus_29(n4locationdata_1_out_30), .bus_30(n4locationdata_1_out_31),
    .bus_31(n4locationdata_1_out_32));
  Multiplexer #(.width(32), .enable("false")) multiplexer_3 (
    .in1(level_installer_1_column), .out(Column), .sel(On_Off));  // open: in0
  Multiplexer #(.width(5), .enable("false")) multiplexer_4 (
    .in1(5'b00111), .out(Y___start), .sel(On_Off));  // open: in0
  Multiplexer #(.width(5), .enable("false")) multiplexer_5 (
    .in1({5{1'b1}}), .out(X___finishTo), .sel(On_Off));  // open: in0
  Multiplexer #(.width(5), .enable("false")) multiplexer_6 (
    .in1(5'b11110), .out(Y___finishTo), .sel(On_Off));  // open: in0
  Multiplexer #(.width(5), .enable("false")) multiplexer_7 (
    .in1({5{1'b1}}), .out(X___finishFrom), .sel(On_Off));  // open: in0
  Multiplexer #(.width(5), .enable("false")) multiplexer_8 (
    .in1(5'b11001), .out(Y___finishFrom), .sel(On_Off));  // open: in0

  // Other names for the same wires on the sheet: do = On_Off

  // Notes on the sheet:
  //   Level Loader
endmodule

module _5location (
  input  Clock,
  input  On_Off,
  output [31:0] Column,
  output [4:0] Number_of_column,
  output [4:0] X___finishTo,
  output [4:0] Y___finishTo,
  output [4:0] X___finishFrom,
  output [4:0] Y___finishFrom,
  output [4:0] X___start,
  output [4:0] Y___start
);

  wire controlled_buffer_1_out, controlled_buffer_2_out, counter_1_carry, not_1_out, not_2_out;
  wire [4:0] counter_2_q;
  wire [31:0] level_installer_1_column, n5locationdata_1_out_1, n5locationdata_1_out_2,
       n5locationdata_1_out_3, n5locationdata_1_out_4, n5locationdata_1_out_5, n5locationdata_1_out_6,
       n5locationdata_1_out_7, n5locationdata_1_out_8, n5locationdata_1_out_9, n5locationdata_1_out_10,
       n5locationdata_1_out_11, n5locationdata_1_out_12, n5locationdata_1_out_13, n5locationdata_1_out_14,
       n5locationdata_1_out_15, n5locationdata_1_out_16, n5locationdata_1_out_17, n5locationdata_1_out_18,
       n5locationdata_1_out_19, n5locationdata_1_out_20, n5locationdata_1_out_21, n5locationdata_1_out_22,
       n5locationdata_1_out_23, n5locationdata_1_out_24, n5locationdata_1_out_25, n5locationdata_1_out_26,
       n5locationdata_1_out_27, n5locationdata_1_out_28, n5locationdata_1_out_29, n5locationdata_1_out_30,
       n5locationdata_1_out_31, n5locationdata_1_out_32;

  not not_1 (not_1_out, counter_1_carry);
  not not_2 (not_2_out, counter_1_carry);
  assign controlled_buffer_1_out = not_2_out ? Clock : 1'bz;  // Controlled_Buffer controlled_buffer_1
  Counter #(.width(6), .max('h3f)) counter_1 (
    .count(controlled_buffer_1_out), .carry(counter_1_carry), .clk(controlled_buffer_1_out));  // open: load, D, Q, clr
  Multiplexer #(.width(5), .enable("false")) multiplexer_1 (
    .in1(counter_2_q), .out(Number_of_column), .sel(On_Off));  // open: in0
  Counter #(.width(5), .max('h1f)) counter_2 (
    .count(controlled_buffer_2_out), .Q(counter_2_q), .clk(controlled_buffer_2_out));  // open: load, D, carry, clr
  assign controlled_buffer_2_out = not_1_out ? Clock : 1'bz;  // Controlled_Buffer controlled_buffer_2
  _5locationData u_5locationdata_1 (
    .out_1(n5locationdata_1_out_1), .out_2(n5locationdata_1_out_2), .out_3(n5locationdata_1_out_3),
    .out_4(n5locationdata_1_out_4), .out_5(n5locationdata_1_out_5), .out_6(n5locationdata_1_out_6),
    .out_7(n5locationdata_1_out_7), .out_8(n5locationdata_1_out_8), .out_9(n5locationdata_1_out_9),
    .out_10(n5locationdata_1_out_10), .out_11(n5locationdata_1_out_11), .out_12(n5locationdata_1_out_12),
    .out_13(n5locationdata_1_out_13), .out_14(n5locationdata_1_out_14), .out_15(n5locationdata_1_out_15),
    .out_16(n5locationdata_1_out_16), .out_17(n5locationdata_1_out_17), .out_18(n5locationdata_1_out_18),
    .out_19(n5locationdata_1_out_19), .out_20(n5locationdata_1_out_20), .out_21(n5locationdata_1_out_21),
    .out_22(n5locationdata_1_out_22), .out_23(n5locationdata_1_out_23), .out_24(n5locationdata_1_out_24),
    .out_25(n5locationdata_1_out_25), .out_26(n5locationdata_1_out_26), .out_27(n5locationdata_1_out_27),
    .out_28(n5locationdata_1_out_28), .out_29(n5locationdata_1_out_29), .out_30(n5locationdata_1_out_30),
    .out_31(n5locationdata_1_out_31), .out_32(n5locationdata_1_out_32));
  Multiplexer #(.width(5), .enable("false")) multiplexer_2 (
    .in1(5'b00010), .out(X___start), .sel(On_Off));  // open: in0
  Level_Installer level_installer_1 (
    .Number_of_column(counter_2_q), .Column(level_installer_1_column), .bus_0(n5locationdata_1_out_1),
    .bus_1(n5locationdata_1_out_2), .bus_2(n5locationdata_1_out_3), .bus_3(n5locationdata_1_out_4),
    .bus_4(n5locationdata_1_out_5), .bus_5(n5locationdata_1_out_6), .bus_6(n5locationdata_1_out_7),
    .bus_7(n5locationdata_1_out_8), .bus_8(n5locationdata_1_out_9), .bus_9(n5locationdata_1_out_10),
    .bus_10(n5locationdata_1_out_11), .bus_11(n5locationdata_1_out_12), .bus_12(n5locationdata_1_out_13),
    .bus_13(n5locationdata_1_out_14), .bus_14(n5locationdata_1_out_15), .bus_15(n5locationdata_1_out_16),
    .bus_16(n5locationdata_1_out_17), .bus_17(n5locationdata_1_out_18), .bus_18(n5locationdata_1_out_19),
    .bus_19(n5locationdata_1_out_20), .bus_20(n5locationdata_1_out_21), .bus_21(n5locationdata_1_out_22),
    .bus_22(n5locationdata_1_out_23), .bus_23(n5locationdata_1_out_24), .bus_24(n5locationdata_1_out_25),
    .bus_25(n5locationdata_1_out_26), .bus_26(n5locationdata_1_out_27), .bus_27(n5locationdata_1_out_28),
    .bus_28(n5locationdata_1_out_29), .bus_29(n5locationdata_1_out_30), .bus_30(n5locationdata_1_out_31),
    .bus_31(n5locationdata_1_out_32));
  Multiplexer #(.width(32), .enable("false")) multiplexer_3 (
    .in1(level_installer_1_column), .out(Column), .sel(On_Off));  // open: in0
  Multiplexer #(.width(5), .enable("false")) multiplexer_4 (
    .in1(5'b00111), .out(Y___start), .sel(On_Off));  // open: in0
  Multiplexer #(.width(5), .enable("false")) multiplexer_5 (
    .in1({5{1'b0}}), .out(X___finishTo), .sel(On_Off));  // open: in0
  Multiplexer #(.width(5), .enable("false")) multiplexer_6 (
    .in1(5'b11110), .out(Y___finishTo), .sel(On_Off));  // open: in0
  Multiplexer #(.width(5), .enable("false")) multiplexer_7 (
    .in1({5{1'b0}}), .out(X___finishFrom), .sel(On_Off));  // open: in0
  Multiplexer #(.width(5), .enable("false")) multiplexer_8 (
    .in1(5'b11001), .out(Y___finishFrom), .sel(On_Off));  // open: in0

  // Other names for the same wires on the sheet: do = On_Off

  // Notes on the sheet:
  //   Level Loader
endmodule

module _5locationData (
  output [31:0] out_1,
  output [31:0] out_2,
  output [31:0] out_3,
  output [31:0] out_4,
  output [31:0] out_5,
  output [31:0] out_6,
  output [31:0] out_7,
  output [31:0] out_8,
  output [31:0] out_9,
  output [31:0] out_10,
  output [31:0] out_11,
  output [31:0] out_12,
  output [31:0] out_13,
  output [31:0] out_14,
  output [31:0] out_15,
  output [31:0] out_16,
  output [31:0] out_17,
  output [31:0] out_18,
  output [31:0] out_19,
  output [31:0] out_20,
  output [31:0] out_21,
  output [31:0] out_22,
  output [31:0] out_23,
  output [31:0] out_24,
  output [31:0] out_25,
  output [31:0] out_26,
  output [31:0] out_27,
  output [31:0] out_28,
  output [31:0] out_29,
  output [31:0] out_30,
  output [31:0] out_31,
  output [31:0] out_32
);


  assign out_1 = 32'h81fffc0f;
  assign out_2 = 32'h81000009;
  assign out_3 = 32'h81000009;
  assign out_4 = 32'h81000009;
  assign out_5 = 32'h80000009;
  assign out_6 = 32'h90000001;
  assign out_7 = 32'h90000001;
  assign out_8 = 32'h82000021;
  assign out_9 = 32'h92000021;
  assign out_10 = 32'h80000001;
  assign out_11 = 32'h80800101;
  assign out_12 = 32'h80100101;
  assign out_13 = 32'h80100801;
  assign out_14 = 32'h80020801;
  assign out_15 = 32'h80024001;
  assign out_16 = 32'h80004001;
  assign out_17 = 32'h80000001;
  assign out_18 = 32'h80000001;
  assign out_19 = 32'h80000001;
  assign out_20 = 32'h80000001;
  assign out_21 = 32'h80000001;
  assign out_22 = 32'h80000001;
  assign out_23 = 32'h80000001;
  assign out_24 = 32'h80000001;
  assign out_25 = 32'h80000001;
  assign out_26 = 32'h80000001;
  assign out_27 = 32'h80000001;
  assign out_28 = 32'h80000001;
  assign out_29 = 32'h80000001;
  assign out_30 = 32'h80000001;
  assign out_31 = 32'h80000001;
  assign out_32 = {32{1'b1}};
endmodule

module _6location (
  input  Clock,
  input  On_Off,
  output [31:0] Column,
  output [4:0] Number_of_column,
  output [4:0] X___finishTo,
  output [4:0] Y___finishTo,
  output [4:0] X___finishFrom,
  output [4:0] Y___finishFrom,
  output [4:0] X___start,
  output [4:0] Y___start
);

  wire controlled_buffer_1_out, controlled_buffer_2_out, counter_1_carry, not_1_out, not_2_out;
  wire [4:0] counter_2_q;
  wire [31:0] level_installer_1_column, n6locationdata_1_out_1, n6locationdata_1_out_2,
       n6locationdata_1_out_3, n6locationdata_1_out_4, n6locationdata_1_out_5, n6locationdata_1_out_6,
       n6locationdata_1_out_7, n6locationdata_1_out_8, n6locationdata_1_out_9, n6locationdata_1_out_10,
       n6locationdata_1_out_11, n6locationdata_1_out_12, n6locationdata_1_out_13, n6locationdata_1_out_14,
       n6locationdata_1_out_15, n6locationdata_1_out_16, n6locationdata_1_out_17, n6locationdata_1_out_18,
       n6locationdata_1_out_19, n6locationdata_1_out_20, n6locationdata_1_out_21, n6locationdata_1_out_22,
       n6locationdata_1_out_23, n6locationdata_1_out_24, n6locationdata_1_out_25, n6locationdata_1_out_26,
       n6locationdata_1_out_27, n6locationdata_1_out_28, n6locationdata_1_out_29, n6locationdata_1_out_30,
       n6locationdata_1_out_31, n6locationdata_1_out_32;

  not not_1 (not_1_out, counter_1_carry);
  not not_2 (not_2_out, counter_1_carry);
  assign controlled_buffer_1_out = not_2_out ? Clock : 1'bz;  // Controlled_Buffer controlled_buffer_1
  Counter #(.width(6), .max('h3f)) counter_1 (
    .count(controlled_buffer_1_out), .carry(counter_1_carry), .clk(controlled_buffer_1_out));  // open: load, D, Q, clr
  Multiplexer #(.width(5), .enable("false")) multiplexer_1 (
    .in1(counter_2_q), .out(Number_of_column), .sel(On_Off));  // open: in0
  Counter #(.width(5), .max('h1f)) counter_2 (
    .count(controlled_buffer_2_out), .Q(counter_2_q), .clk(controlled_buffer_2_out));  // open: load, D, carry, clr
  assign controlled_buffer_2_out = not_1_out ? Clock : 1'bz;  // Controlled_Buffer controlled_buffer_2
  _6locationData u_6locationdata_1 (
    .out_1(n6locationdata_1_out_1), .out_2(n6locationdata_1_out_2), .out_3(n6locationdata_1_out_3),
    .out_4(n6locationdata_1_out_4), .out_5(n6locationdata_1_out_5), .out_6(n6locationdata_1_out_6),
    .out_7(n6locationdata_1_out_7), .out_8(n6locationdata_1_out_8), .out_9(n6locationdata_1_out_9),
    .out_10(n6locationdata_1_out_10), .out_11(n6locationdata_1_out_11), .out_12(n6locationdata_1_out_12),
    .out_13(n6locationdata_1_out_13), .out_14(n6locationdata_1_out_14), .out_15(n6locationdata_1_out_15),
    .out_16(n6locationdata_1_out_16), .out_17(n6locationdata_1_out_17), .out_18(n6locationdata_1_out_18),
    .out_19(n6locationdata_1_out_19), .out_20(n6locationdata_1_out_20), .out_21(n6locationdata_1_out_21),
    .out_22(n6locationdata_1_out_22), .out_23(n6locationdata_1_out_23), .out_24(n6locationdata_1_out_24),
    .out_25(n6locationdata_1_out_25), .out_26(n6locationdata_1_out_26), .out_27(n6locationdata_1_out_27),
    .out_28(n6locationdata_1_out_28), .out_29(n6locationdata_1_out_29), .out_30(n6locationdata_1_out_30),
    .out_31(n6locationdata_1_out_31), .out_32(n6locationdata_1_out_32));
  Multiplexer #(.width(5), .enable("false")) multiplexer_2 (
    .in1(5'b11101), .out(X___start), .sel(On_Off));  // open: in0
  Level_Installer level_installer_1 (
    .Number_of_column(counter_2_q), .Column(level_installer_1_column), .bus_0(n6locationdata_1_out_1),
    .bus_1(n6locationdata_1_out_2), .bus_2(n6locationdata_1_out_3), .bus_3(n6locationdata_1_out_4),
    .bus_4(n6locationdata_1_out_5), .bus_5(n6locationdata_1_out_6), .bus_6(n6locationdata_1_out_7),
    .bus_7(n6locationdata_1_out_8), .bus_8(n6locationdata_1_out_9), .bus_9(n6locationdata_1_out_10),
    .bus_10(n6locationdata_1_out_11), .bus_11(n6locationdata_1_out_12), .bus_12(n6locationdata_1_out_13),
    .bus_13(n6locationdata_1_out_14), .bus_14(n6locationdata_1_out_15), .bus_15(n6locationdata_1_out_16),
    .bus_16(n6locationdata_1_out_17), .bus_17(n6locationdata_1_out_18), .bus_18(n6locationdata_1_out_19),
    .bus_19(n6locationdata_1_out_20), .bus_20(n6locationdata_1_out_21), .bus_21(n6locationdata_1_out_22),
    .bus_22(n6locationdata_1_out_23), .bus_23(n6locationdata_1_out_24), .bus_24(n6locationdata_1_out_25),
    .bus_25(n6locationdata_1_out_26), .bus_26(n6locationdata_1_out_27), .bus_27(n6locationdata_1_out_28),
    .bus_28(n6locationdata_1_out_29), .bus_29(n6locationdata_1_out_30), .bus_30(n6locationdata_1_out_31),
    .bus_31(n6locationdata_1_out_32));
  Multiplexer #(.width(32), .enable("false")) multiplexer_3 (
    .in1(level_installer_1_column), .out(Column), .sel(On_Off));  // open: in0
  Multiplexer #(.width(5), .enable("false")) multiplexer_4 (
    .in1(5'b11100), .out(Y___start), .sel(On_Off));  // open: in0
  Multiplexer #(.width(5), .enable("false")) multiplexer_5 (
    .in1(5'b10001), .out(X___finishTo), .sel(On_Off));  // open: in0
  Multiplexer #(.width(5), .enable("false")) multiplexer_6 (
    .in1(5'b00101), .out(Y___finishTo), .sel(On_Off));  // open: in0
  Multiplexer #(.width(5), .enable("false")) multiplexer_7 (
    .in1(5'b01001), .out(X___finishFrom), .sel(On_Off));  // open: in0
  Multiplexer #(.width(5), .enable("false")) multiplexer_8 (
    .in1(5'b00100), .out(Y___finishFrom), .sel(On_Off));  // open: in0

  // Other names for the same wires on the sheet: do = On_Off

  // Notes on the sheet:
  //   Level Loader
endmodule

module _6locationData (
  output [31:0] out_1,
  output [31:0] out_2,
  output [31:0] out_3,
  output [31:0] out_4,
  output [31:0] out_5,
  output [31:0] out_6,
  output [31:0] out_7,
  output [31:0] out_8,
  output [31:0] out_9,
  output [31:0] out_10,
  output [31:0] out_11,
  output [31:0] out_12,
  output [31:0] out_13,
  output [31:0] out_14,
  output [31:0] out_15,
  output [31:0] out_16,
  output [31:0] out_17,
  output [31:0] out_18,
  output [31:0] out_19,
  output [31:0] out_20,
  output [31:0] out_21,
  output [31:0] out_22,
  output [31:0] out_23,
  output [31:0] out_24,
  output [31:0] out_25,
  output [31:0] out_26,
  output [31:0] out_27,
  output [31:0] out_28,
  output [31:0] out_29,
  output [31:0] out_30,
  output [31:0] out_31,
  output [31:0] out_32
);


  assign out_1 = {32{1'b1}};
  assign out_2 = 32'h80000001;
  assign out_3 = 32'h80000001;
  assign out_4 = 32'h80000001;
  assign out_5 = 32'h80200001;
  assign out_6 = 32'h80200001;
  assign out_7 = 32'h8121ffe1;
  assign out_8 = 32'h83010461;
  assign out_9 = 32'h86110839;
  assign out_10 = 32'h84110809;
  assign out_11 = 32'h8401080f;
  assign out_12 = 32'h84080809;
  assign out_13 = 32'h84088709;
  assign out_14 = 32'h84020009;
  assign out_15 = 32'h84020709;
  assign out_16 = 32'h86020809;
  assign out_17 = 32'h8302080f;
  assign out_18 = 32'h81020809;
  assign out_19 = 32'h81020839;
  assign out_20 = 32'h81020461;
  assign out_21 = 32'h8103ffe1;
  assign out_22 = 32'h87000001;
  assign out_23 = 32'h84000001;
  assign out_24 = 32'h84000001;
  assign out_25 = 32'h84000001;
  assign out_26 = 32'h87000001;
  assign out_27 = 32'h81000001;
  assign out_28 = 32'h81000001;
  assign out_29 = 32'h81000001;
  assign out_30 = 32'h81000001;
  assign out_31 = 32'h81000001;
  assign out_32 = 32'h81ffffff;
endmodule
module _7location (
  input  Clock,
  input  On_Off,
  output [31:0] Column,
  output [4:0] Number_of_column,
  output [4:0] X___finishTo,
  output [4:0] Y___finishTo,
  output [4:0] X___finishFrom,
  output [4:0] Y___finishFrom,
  output [4:0] X___start,
  output [4:0] Y___start
);

  wire controlled_buffer_1_out, controlled_buffer_2_out, counter_1_carry, not_1_out, not_2_out;
  wire [4:0] counter_2_q;
  wire [31:0] level_installer_1_column, n7locationdata_1_out_1, n7locationdata_1_out_2,
       n7locationdata_1_out_3, n7locationdata_1_out_4, n7locationdata_1_out_5, n7locationdata_1_out_6,
       n7locationdata_1_out_7, n7locationdata_1_out_8, n7locationdata_1_out_9, n7locationdata_1_out_10,
       n7locationdata_1_out_11, n7locationdata_1_out_12, n7locationdata_1_out_13, n7locationdata_1_out_14,
       n7locationdata_1_out_15, n7locationdata_1_out_16, n7locationdata_1_out_17, n7locationdata_1_out_18,
       n7locationdata_1_out_19, n7locationdata_1_out_20, n7locationdata_1_out_21, n7locationdata_1_out_22,
       n7locationdata_1_out_23, n7locationdata_1_out_24, n7locationdata_1_out_25, n7locationdata_1_out_26,
       n7locationdata_1_out_27, n7locationdata_1_out_28, n7locationdata_1_out_29, n7locationdata_1_out_30,
       n7locationdata_1_out_31, n7locationdata_1_out_32;

  not not_1 (not_1_out, counter_1_carry);
  not not_2 (not_2_out, counter_1_carry);
  assign controlled_buffer_1_out = not_2_out ? Clock : 1'bz;  // Controlled_Buffer controlled_buffer_1
  Counter #(.width(6), .max('h3f)) counter_1 (
    .count(controlled_buffer_1_out), .carry(counter_1_carry), .clk(controlled_buffer_1_out));  // open: load, D, Q, clr
  Multiplexer #(.width(5), .enable("false")) multiplexer_1 (
    .in1(counter_2_q), .out(Number_of_column), .sel(On_Off));  // open: in0
  Counter #(.width(5), .max('h1f)) counter_2 (
    .count(controlled_buffer_2_out), .Q(counter_2_q), .clk(controlled_buffer_2_out));  // open: load, D, carry, clr
  assign controlled_buffer_2_out = not_1_out ? Clock : 1'bz;  // Controlled_Buffer controlled_buffer_2
  _7locationData u_7locationdata_1 (
    .out_1(n7locationdata_1_out_1), .out_2(n7locationdata_1_out_2), .out_3(n7locationdata_1_out_3),
    .out_4(n7locationdata_1_out_4), .out_5(n7locationdata_1_out_5), .out_6(n7locationdata_1_out_6),
    .out_7(n7locationdata_1_out_7), .out_8(n7locationdata_1_out_8), .out_9(n7locationdata_1_out_9),
    .out_10(n7locationdata_1_out_10), .out_11(n7locationdata_1_out_11), .out_12(n7locationdata_1_out_12),
    .out_13(n7locationdata_1_out_13), .out_14(n7locationdata_1_out_14), .out_15(n7locationdata_1_out_15),
    .out_16(n7locationdata_1_out_16), .out_17(n7locationdata_1_out_17), .out_18(n7locationdata_1_out_18),
    .out_19(n7locationdata_1_out_19), .out_20(n7locationdata_1_out_20), .out_21(n7locationdata_1_out_21),
    .out_22(n7locationdata_1_out_22), .out_23(n7locationdata_1_out_23), .out_24(n7locationdata_1_out_24),
    .out_25(n7locationdata_1_out_25), .out_26(n7locationdata_1_out_26), .out_27(n7locationdata_1_out_27),
    .out_28(n7locationdata_1_out_28), .out_29(n7locationdata_1_out_29), .out_30(n7locationdata_1_out_30),
    .out_31(n7locationdata_1_out_31), .out_32(n7locationdata_1_out_32));
  Multiplexer #(.width(5), .enable("false")) multiplexer_2 (
    .in1(5'b01110), .out(X___start), .sel(On_Off));  // open: in0
  Level_Installer level_installer_1 (
    .Number_of_column(counter_2_q), .Column(level_installer_1_column), .bus_0(n7locationdata_1_out_1),
    .bus_1(n7locationdata_1_out_2), .bus_2(n7locationdata_1_out_3), .bus_3(n7locationdata_1_out_4),
    .bus_4(n7locationdata_1_out_5), .bus_5(n7locationdata_1_out_6), .bus_6(n7locationdata_1_out_7),
    .bus_7(n7locationdata_1_out_8), .bus_8(n7locationdata_1_out_9), .bus_9(n7locationdata_1_out_10),
    .bus_10(n7locationdata_1_out_11), .bus_11(n7locationdata_1_out_12), .bus_12(n7locationdata_1_out_13),
    .bus_13(n7locationdata_1_out_14), .bus_14(n7locationdata_1_out_15), .bus_15(n7locationdata_1_out_16),
    .bus_16(n7locationdata_1_out_17), .bus_17(n7locationdata_1_out_18), .bus_18(n7locationdata_1_out_19),
    .bus_19(n7locationdata_1_out_20), .bus_20(n7locationdata_1_out_21), .bus_21(n7locationdata_1_out_22),
    .bus_22(n7locationdata_1_out_23), .bus_23(n7locationdata_1_out_24), .bus_24(n7locationdata_1_out_25),
    .bus_25(n7locationdata_1_out_26), .bus_26(n7locationdata_1_out_27), .bus_27(n7locationdata_1_out_28),
    .bus_28(n7locationdata_1_out_29), .bus_29(n7locationdata_1_out_30), .bus_30(n7locationdata_1_out_31),
    .bus_31(n7locationdata_1_out_32));
  Multiplexer #(.width(32), .enable("false")) multiplexer_3 (
    .in1(level_installer_1_column), .out(Column), .sel(On_Off));  // open: in0
  Multiplexer #(.width(5), .enable("false")) multiplexer_4 (
    .in1(5'b11110), .out(Y___start), .sel(On_Off));  // open: in0
  Multiplexer #(.width(5), .enable("false")) multiplexer_5 (
    .in1({5{1'b0}}), .out(X___finishTo), .sel(On_Off));  // open: in0
  Multiplexer #(.width(5), .enable("false")) multiplexer_6 (
    .in1(5'b01111), .out(Y___finishTo), .sel(On_Off));  // open: in0
  Multiplexer #(.width(5), .enable("false")) multiplexer_7 (
    .in1({5{1'b0}}), .out(X___finishFrom), .sel(On_Off));  // open: in0
  Multiplexer #(.width(5), .enable("false")) multiplexer_8 (
    .in1(5'b01110), .out(Y___finishFrom), .sel(On_Off));  // open: in0

  // Other names for the same wires on the sheet: do = On_Off

  // Notes on the sheet:
  //   Level Loader
endmodule

module _7locationData (
  output [31:0] out_1,
  output [31:0] out_2,
  output [31:0] out_3,
  output [31:0] out_4,
  output [31:0] out_5,
  output [31:0] out_6,
  output [31:0] out_7,
  output [31:0] out_8,
  output [31:0] out_9,
  output [31:0] out_10,
  output [31:0] out_11,
  output [31:0] out_12,
  output [31:0] out_13,
  output [31:0] out_14,
  output [31:0] out_15,
  output [31:0] out_16,
  output [31:0] out_17,
  output [31:0] out_18,
  output [31:0] out_19,
  output [31:0] out_20,
  output [31:0] out_21,
  output [31:0] out_22,
  output [31:0] out_23,
  output [31:0] out_24,
  output [31:0] out_25,
  output [31:0] out_26,
  output [31:0] out_27,
  output [31:0] out_28,
  output [31:0] out_29,
  output [31:0] out_30,
  output [31:0] out_31,
  output [31:0] out_32
);


  assign out_1 = 32'hffff3fff;
  assign out_2 = 32'h80000001;
  assign out_3 = 32'h80000001;
  assign out_4 = 32'h80000001;
  assign out_5 = 32'h80000001;
  assign out_6 = 32'h80004001;
  assign out_7 = 32'h80000001;
  assign out_8 = 32'h80000001;
  assign out_9 = 32'h80010001;
  assign out_10 = 32'h80000001;
  assign out_11 = 32'h80000001;
  assign out_12 = 32'h80000001;
  assign out_13 = 32'h10001;
  assign out_14 = 32'h1000001;
  assign out_15 = 32'h1;
  assign out_16 = 32'h4001;
  assign out_17 = 32'h1;
  assign out_18 = 32'h200001;
  assign out_19 = 32'h1;
  assign out_20 = 32'h8001;
  assign out_21 = 32'h1;
  assign out_22 = 32'h80080001;
  assign out_23 = 32'h80000001;
  assign out_24 = 32'h80000001;
  assign out_25 = 32'h80000001;
  assign out_26 = 32'h80000001;
  assign out_27 = 32'h80000001;
  assign out_28 = 32'h80000001;
  assign out_29 = 32'h80000001;
  assign out_30 = 32'h80000001;
  assign out_31 = 32'h80000001;
  assign out_32 = {32{1'b1}};
endmodule

module _8locationData (
  output [31:0] out_1,
  output [31:0] out_2,
  output [31:0] out_3,
  output [31:0] out_4,
  output [31:0] out_5,
  output [31:0] out_6,
  output [31:0] out_7,
  output [31:0] out_8,
  output [31:0] out_9,
  output [31:0] out_10,
  output [31:0] out_11,
  output [31:0] out_12,
  output [31:0] out_13,
  output [31:0] out_14,
  output [31:0] out_15,
  output [31:0] out_16,
  output [31:0] out_17,
  output [31:0] out_18,
  output [31:0] out_19,
  output [31:0] out_20,
  output [31:0] out_21,
  output [31:0] out_22,
  output [31:0] out_23,
  output [31:0] out_24,
  output [31:0] out_25,
  output [31:0] out_26,
  output [31:0] out_27,
  output [31:0] out_28,
  output [31:0] out_29,
  output [31:0] out_30,
  output [31:0] out_31,
  output [31:0] out_32
);


  assign out_1 = {32{1'b1}};
  assign out_2 = 32'h80008001;
  assign out_3 = 32'h80008001;
  assign out_4 = 32'h80001001;
  assign out_5 = 32'h80041001;
  assign out_6 = 32'h80040001;
  assign out_7 = 32'h80000001;
  assign out_8 = 32'h80000401;
  assign out_9 = 32'h80100401;
  assign out_10 = 32'h80100001;
  assign out_11 = 32'h80000001;
  assign out_12 = 32'h80000001;
  assign out_13 = 32'h80000001;
  assign out_14 = 32'h80000401;
  assign out_15 = 32'h80100401;
  assign out_16 = 32'h80100001;
  assign out_17 = 32'h80000001;
  assign out_18 = 32'h80000001;
  assign out_19 = 32'h80100801;
  assign out_20 = 32'h80100001;
  assign out_21 = 32'h80000201;
  assign out_22 = 32'h80000001;
  assign out_23 = 32'h80100081;
  assign out_24 = 32'h80100001;
  assign out_25 = 32'h80000001;
  assign out_26 = 32'h80000021;
  assign out_27 = 32'h80400031;
  assign out_28 = 32'h80000011;
  assign out_29 = 32'h81000011;
  assign out_30 = 32'h80000011;
  assign out_31 = 32'h80000011;
  assign out_32 = 32'hc3ffff9f;
endmodule

module _8location (
  input  Clock,
  input  On_Off,
  output [31:0] Column,
  output [4:0] Number_of_column,
  output [4:0] X___finishTo,
  output [4:0] Y___finishTo,
  output [4:0] X___finishFrom,
  output [4:0] Y___finishFrom,
  output [4:0] X___start,
  output [4:0] Y___start
);

  wire controlled_buffer_1_out, controlled_buffer_2_out, counter_1_carry, not_1_out, not_2_out;
  wire [4:0] counter_2_q;
  wire [31:0] level_installer_1_column, n8locationdata_1_out_1, n8locationdata_1_out_2,
       n8locationdata_1_out_3, n8locationdata_1_out_4, n8locationdata_1_out_5, n8locationdata_1_out_6,
       n8locationdata_1_out_7, n8locationdata_1_out_8, n8locationdata_1_out_9, n8locationdata_1_out_10,
       n8locationdata_1_out_11, n8locationdata_1_out_12, n8locationdata_1_out_13, n8locationdata_1_out_14,
       n8locationdata_1_out_15, n8locationdata_1_out_16, n8locationdata_1_out_17, n8locationdata_1_out_18,
       n8locationdata_1_out_19, n8locationdata_1_out_20, n8locationdata_1_out_21, n8locationdata_1_out_22,
       n8locationdata_1_out_23, n8locationdata_1_out_24, n8locationdata_1_out_25, n8locationdata_1_out_26,
       n8locationdata_1_out_27, n8locationdata_1_out_28, n8locationdata_1_out_29, n8locationdata_1_out_30,
       n8locationdata_1_out_31, n8locationdata_1_out_32;

  not not_1 (not_1_out, counter_1_carry);
  not not_2 (not_2_out, counter_1_carry);
  assign controlled_buffer_1_out = not_2_out ? Clock : 1'bz;  // Controlled_Buffer controlled_buffer_1
  Counter #(.width(6), .max('h3f)) counter_1 (
    .count(controlled_buffer_1_out), .carry(counter_1_carry), .clk(controlled_buffer_1_out));  // open: load, D, Q, clr
  Multiplexer #(.width(5), .enable("false")) multiplexer_1 (
    .in1(counter_2_q), .out(Number_of_column), .sel(On_Off));  // open: in0
  Counter #(.width(5), .max('h1f)) counter_2 (
    .count(controlled_buffer_2_out), .Q(counter_2_q), .clk(controlled_buffer_2_out));  // open: load, D, carry, clr
  assign controlled_buffer_2_out = not_1_out ? Clock : 1'bz;  // Controlled_Buffer controlled_buffer_2
  _8locationData u_8locationdata_1 (
    .out_1(n8locationdata_1_out_1), .out_2(n8locationdata_1_out_2), .out_3(n8locationdata_1_out_3),
    .out_4(n8locationdata_1_out_4), .out_5(n8locationdata_1_out_5), .out_6(n8locationdata_1_out_6),
    .out_7(n8locationdata_1_out_7), .out_8(n8locationdata_1_out_8), .out_9(n8locationdata_1_out_9),
    .out_10(n8locationdata_1_out_10), .out_11(n8locationdata_1_out_11), .out_12(n8locationdata_1_out_12),
    .out_13(n8locationdata_1_out_13), .out_14(n8locationdata_1_out_14), .out_15(n8locationdata_1_out_15),
    .out_16(n8locationdata_1_out_16), .out_17(n8locationdata_1_out_17), .out_18(n8locationdata_1_out_18),
    .out_19(n8locationdata_1_out_19), .out_20(n8locationdata_1_out_20), .out_21(n8locationdata_1_out_21),
    .out_22(n8locationdata_1_out_22), .out_23(n8locationdata_1_out_23), .out_24(n8locationdata_1_out_24),
    .out_25(n8locationdata_1_out_25), .out_26(n8locationdata_1_out_26), .out_27(n8locationdata_1_out_27),
    .out_28(n8locationdata_1_out_28), .out_29(n8locationdata_1_out_29), .out_30(n8locationdata_1_out_30),
    .out_31(n8locationdata_1_out_31), .out_32(n8locationdata_1_out_32));
  Multiplexer #(.width(5), .enable("false")) multiplexer_2 (
    .in1(5'b11100), .out(X___start), .sel(On_Off));  // open: in0
  Level_Installer level_installer_1 (
    .Number_of_column(counter_2_q), .Column(level_installer_1_column), .bus_0(n8locationdata_1_out_1),
    .bus_1(n8locationdata_1_out_2), .bus_2(n8locationdata_1_out_3), .bus_3(n8locationdata_1_out_4),
    .bus_4(n8locationdata_1_out_5), .bus_5(n8locationdata_1_out_6), .bus_6(n8locationdata_1_out_7),
    .bus_7(n8locationdata_1_out_8), .bus_8(n8locationdata_1_out_9), .bus_9(n8locationdata_1_out_10),
    .bus_10(n8locationdata_1_out_11), .bus_11(n8locationdata_1_out_12), .bus_12(n8locationdata_1_out_13),
    .bus_13(n8locationdata_1_out_14), .bus_14(n8locationdata_1_out_15), .bus_15(n8locationdata_1_out_16),
    .bus_16(n8locationdata_1_out_17), .bus_17(n8locationdata_1_out_18), .bus_18(n8locationdata_1_out_19),
    .bus_19(n8locationdata_1_out_20), .bus_20(n8locationdata_1_out_21), .bus_21(n8locationdata_1_out_22),
    .bus_22(n8locationdata_1_out_23), .bus_23(n8locationdata_1_out_24), .bus_24(n8locationdata_1_out_25),
    .bus_25(n8locationdata_1_out_26), .bus_26(n8locationdata_1_out_27), .bus_27(n8locationdata_1_out_28),
    .bus_28(n8locationdata_1_out_29), .bus_29(n8locationdata_1_out_30), .bus_30(n8locationdata_1_out_31),
    .bus_31(n8locationdata_1_out_32));
  Multiplexer #(.width(32), .enable("false")) multiplexer_3 (
    .in1(level_installer_1_column), .out(Column), .sel(On_Off));  // open: in0
  Multiplexer #(.width(5), .enable("false")) multiplexer_4 (
    .in1(5'b01000), .out(Y___start), .sel(On_Off));  // open: in0
  Multiplexer #(.width(5), .enable("false")) multiplexer_5 (
    .in1({5{1'b1}}), .out(X___finishTo), .sel(On_Off));  // open: in0
  Multiplexer #(.width(5), .enable("false")) multiplexer_6 (
    .in1(5'b11101), .out(Y___finishTo), .sel(On_Off));  // open: in0
  Multiplexer #(.width(5), .enable("false")) multiplexer_7 (
    .in1({5{1'b1}}), .out(X___finishFrom), .sel(On_Off));  // open: in0
  Multiplexer #(.width(5), .enable("false")) multiplexer_8 (
    .in1(5'b11010), .out(Y___finishFrom), .sel(On_Off));  // open: in0

  // Other names for the same wires on the sheet: do = On_Off

  // Notes on the sheet:
  //   Level Loader
endmodule

module _9location (
  input  Clock,
  input  On_Off,
  output [31:0] Column,
  output [4:0] Number_of_column,
  output [4:0] X___finishTo,
  output [4:0] Y___finishTo,
  output [4:0] X___finishFrom,
  output [4:0] Y___finishFrom,
  output [4:0] X___start,
  output [4:0] Y___start
);

  wire controlled_buffer_1_out, controlled_buffer_2_out, counter_1_carry, not_1_out, not_2_out;
  wire [4:0] counter_2_q;
  wire [31:0] level_installer_1_column, n9locationdata_1_out_1, n9locationdata_1_out_2,
       n9locationdata_1_out_3, n9locationdata_1_out_4, n9locationdata_1_out_5, n9locationdata_1_out_6,
       n9locationdata_1_out_7, n9locationdata_1_out_8, n9locationdata_1_out_9, n9locationdata_1_out_10,
       n9locationdata_1_out_11, n9locationdata_1_out_12, n9locationdata_1_out_13, n9locationdata_1_out_14,
       n9locationdata_1_out_15, n9locationdata_1_out_16, n9locationdata_1_out_17, n9locationdata_1_out_18,
       n9locationdata_1_out_19, n9locationdata_1_out_20, n9locationdata_1_out_21, n9locationdata_1_out_22,
       n9locationdata_1_out_23, n9locationdata_1_out_24, n9locationdata_1_out_25, n9locationdata_1_out_26,
       n9locationdata_1_out_27, n9locationdata_1_out_28, n9locationdata_1_out_29, n9locationdata_1_out_30,
       n9locationdata_1_out_31, n9locationdata_1_out_32;

  not not_1 (not_1_out, counter_1_carry);
  not not_2 (not_2_out, counter_1_carry);
  assign controlled_buffer_1_out = not_2_out ? Clock : 1'bz;  // Controlled_Buffer controlled_buffer_1
  Counter #(.width(6), .max('h3f)) counter_1 (
    .count(controlled_buffer_1_out), .carry(counter_1_carry), .clk(controlled_buffer_1_out));  // open: load, D, Q, clr
  Multiplexer #(.width(5), .enable("false")) multiplexer_1 (
    .in1(counter_2_q), .out(Number_of_column), .sel(On_Off));  // open: in0
  Counter #(.width(5), .max('h1f)) counter_2 (
    .count(controlled_buffer_2_out), .Q(counter_2_q), .clk(controlled_buffer_2_out));  // open: load, D, carry, clr
  assign controlled_buffer_2_out = not_1_out ? Clock : 1'bz;  // Controlled_Buffer controlled_buffer_2
  _9locationData u_9locationdata_1 (
    .out_1(n9locationdata_1_out_1), .out_2(n9locationdata_1_out_2), .out_3(n9locationdata_1_out_3),
    .out_4(n9locationdata_1_out_4), .out_5(n9locationdata_1_out_5), .out_6(n9locationdata_1_out_6),
    .out_7(n9locationdata_1_out_7), .out_8(n9locationdata_1_out_8), .out_9(n9locationdata_1_out_9),
    .out_10(n9locationdata_1_out_10), .out_11(n9locationdata_1_out_11), .out_12(n9locationdata_1_out_12),
    .out_13(n9locationdata_1_out_13), .out_14(n9locationdata_1_out_14), .out_15(n9locationdata_1_out_15),
    .out_16(n9locationdata_1_out_16), .out_17(n9locationdata_1_out_17), .out_18(n9locationdata_1_out_18),
    .out_19(n9locationdata_1_out_19), .out_20(n9locationdata_1_out_20), .out_21(n9locationdata_1_out_21),
    .out_22(n9locationdata_1_out_22), .out_23(n9locationdata_1_out_23), .out_24(n9locationdata_1_out_24),
    .out_25(n9locationdata_1_out_25), .out_26(n9locationdata_1_out_26), .out_27(n9locationdata_1_out_27),
    .out_28(n9locationdata_1_out_28), .out_29(n9locationdata_1_out_29), .out_30(n9locationdata_1_out_30),
    .out_31(n9locationdata_1_out_31), .out_32(n9locationdata_1_out_32));
  Multiplexer #(.width(5), .enable("false")) multiplexer_2 (
    .in1(5'b00011), .out(X___start), .sel(On_Off));  // open: in0
  Level_Installer level_installer_1 (
    .Number_of_column(counter_2_q), .Column(level_installer_1_column), .bus_0(n9locationdata_1_out_1),
    .bus_1(n9locationdata_1_out_2), .bus_2(n9locationdata_1_out_3), .bus_3(n9locationdata_1_out_4),
    .bus_4(n9locationdata_1_out_5), .bus_5(n9locationdata_1_out_6), .bus_6(n9locationdata_1_out_7),
    .bus_7(n9locationdata_1_out_8), .bus_8(n9locationdata_1_out_9), .bus_9(n9locationdata_1_out_10),
    .bus_10(n9locationdata_1_out_11), .bus_11(n9locationdata_1_out_12), .bus_12(n9locationdata_1_out_13),
    .bus_13(n9locationdata_1_out_14), .bus_14(n9locationdata_1_out_15), .bus_15(n9locationdata_1_out_16),
    .bus_16(n9locationdata_1_out_17), .bus_17(n9locationdata_1_out_18), .bus_18(n9locationdata_1_out_19),
    .bus_19(n9locationdata_1_out_20), .bus_20(n9locationdata_1_out_21), .bus_21(n9locationdata_1_out_22),
    .bus_22(n9locationdata_1_out_23), .bus_23(n9locationdata_1_out_24), .bus_24(n9locationdata_1_out_25),
    .bus_25(n9locationdata_1_out_26), .bus_26(n9locationdata_1_out_27), .bus_27(n9locationdata_1_out_28),
    .bus_28(n9locationdata_1_out_29), .bus_29(n9locationdata_1_out_30), .bus_30(n9locationdata_1_out_31),
    .bus_31(n9locationdata_1_out_32));
  Multiplexer #(.width(32), .enable("false")) multiplexer_3 (
    .in1(level_installer_1_column), .out(Column), .sel(On_Off));  // open: in0
  Multiplexer #(.width(5), .enable("false")) multiplexer_4 (
    .in1(5'b11011), .out(Y___start), .sel(On_Off));  // open: in0
  Multiplexer #(.width(5), .enable("false")) multiplexer_5 (
    .in1({5{1'b0}}), .out(X___finishTo), .sel(On_Off));  // open: in0
  Multiplexer #(.width(5), .enable("false")) multiplexer_6 (
    .in1(5'b01000), .out(Y___finishTo), .sel(On_Off));  // open: in0
  Multiplexer #(.width(5), .enable("false")) multiplexer_7 (
    .in1({5{1'b0}}), .out(X___finishFrom), .sel(On_Off));  // open: in0
  Multiplexer #(.width(5), .enable("false")) multiplexer_8 (
    .in1(5'b00100), .out(Y___finishFrom), .sel(On_Off));  // open: in0

  // Other names for the same wires on the sheet: do = On_Off

  // Notes on the sheet:
  //   Level Loader
endmodule

module _9locationData (
  output [31:0] out_1,
  output [31:0] out_2,
  output [31:0] out_3,
  output [31:0] out_4,
  output [31:0] out_5,
  output [31:0] out_6,
  output [31:0] out_7,
  output [31:0] out_8,
  output [31:0] out_9,
  output [31:0] out_10,
  output [31:0] out_11,
  output [31:0] out_12,
  output [31:0] out_13,
  output [31:0] out_14,
  output [31:0] out_15,
  output [31:0] out_16,
  output [31:0] out_17,
  output [31:0] out_18,
  output [31:0] out_19,
  output [31:0] out_20,
  output [31:0] out_21,
  output [31:0] out_22,
  output [31:0] out_23,
  output [31:0] out_24,
  output [31:0] out_25,
  output [31:0] out_26,
  output [31:0] out_27,
  output [31:0] out_28,
  output [31:0] out_29,
  output [31:0] out_30,
  output [31:0] out_31,
  output [31:0] out_32
);


  assign out_1 = 32'hc1fffe0f;
  assign out_2 = 32'h81000001;
  assign out_3 = 32'h81000001;
  assign out_4 = 32'h81000001;
  assign out_5 = 32'h81000001;
  assign out_6 = 32'h81000001;
  assign out_7 = 32'h81000001;
  assign out_8 = 32'h81000201;
  assign out_9 = 32'h81ffc201;
  assign out_10 = 32'h80894401;
  assign out_11 = 32'h80894801;
  assign out_12 = 32'h80001001;
  assign out_13 = 32'h8022a001;
  assign out_14 = 32'h8022a001;
  assign out_15 = 32'hffffe001;
  assign out_16 = 32'h80000001;
  assign out_17 = 32'h80000001;
  assign out_18 = 32'h80000001;
  assign out_19 = 32'h80000001;
  assign out_20 = 32'h80000001;
  assign out_21 = 32'h80000001;
  assign out_22 = 32'h80000001;
  assign out_23 = 32'h80000001;
  assign out_24 = 32'h80000001;
  assign out_25 = 32'h80000001;
  assign out_26 = 32'h80000001;
  assign out_27 = 32'h80000001;
  assign out_28 = 32'h80000001;
  assign out_29 = 32'h80000001;
  assign out_30 = 32'h80000001;
  assign out_31 = 32'h80000001;
  assign out_32 = {32{1'b1}};
endmodule

module _10location (
  input  Clock,
  input  On_Off,
  output [31:0] Column,
  output [4:0] Number_of_column,
  output [4:0] X___finishTo,
  output [4:0] Y___finishTo,
  output [4:0] X___finishFrom,
  output [4:0] Y___finishFrom,
  output [4:0] X___start,
  output [4:0] Y___start
);

  wire controlled_buffer_1_out, controlled_buffer_2_out, counter_1_carry, not_1_out, not_2_out;
  wire [4:0] counter_2_q;
  wire [31:0] level_installer_1_column, n10locationdata_1_out_1, n10locationdata_1_out_2,
       n10locationdata_1_out_3, n10locationdata_1_out_4, n10locationdata_1_out_5, n10locationdata_1_out_6,
       n10locationdata_1_out_7, n10locationdata_1_out_8, n10locationdata_1_out_9, n10locationdata_1_out_10,
       n10locationdata_1_out_11, n10locationdata_1_out_12, n10locationdata_1_out_13,
       n10locationdata_1_out_14, n10locationdata_1_out_15, n10locationdata_1_out_16,
       n10locationdata_1_out_17, n10locationdata_1_out_18, n10locationdata_1_out_19,
       n10locationdata_1_out_20, n10locationdata_1_out_21, n10locationdata_1_out_22,
       n10locationdata_1_out_23, n10locationdata_1_out_24, n10locationdata_1_out_25,
       n10locationdata_1_out_26, n10locationdata_1_out_27, n10locationdata_1_out_28,
       n10locationdata_1_out_29, n10locationdata_1_out_30, n10locationdata_1_out_31, n10locationdata_1_out_32;

  not not_1 (not_1_out, counter_1_carry);
  not not_2 (not_2_out, counter_1_carry);
  assign controlled_buffer_1_out = not_2_out ? Clock : 1'bz;  // Controlled_Buffer controlled_buffer_1
  Counter #(.width(6), .max('h3f)) counter_1 (
    .count(controlled_buffer_1_out), .carry(counter_1_carry), .clk(controlled_buffer_1_out));  // open: load, D, Q, clr
  Multiplexer #(.width(5), .enable("false")) multiplexer_1 (
    .in1(counter_2_q), .out(Number_of_column), .sel(On_Off));  // open: in0
  Counter #(.width(5), .max('h1f)) counter_2 (
    .count(controlled_buffer_2_out), .Q(counter_2_q), .clk(controlled_buffer_2_out));  // open: load, D, carry, clr
  assign controlled_buffer_2_out = not_1_out ? Clock : 1'bz;  // Controlled_Buffer controlled_buffer_2
  _10locationData u_10locationdata_1 (
    .out_1(n10locationdata_1_out_1), .out_2(n10locationdata_1_out_2), .out_3(n10locationdata_1_out_3),
    .out_4(n10locationdata_1_out_4), .out_5(n10locationdata_1_out_5), .out_6(n10locationdata_1_out_6),
    .out_7(n10locationdata_1_out_7), .out_8(n10locationdata_1_out_8), .out_9(n10locationdata_1_out_9),
    .out_10(n10locationdata_1_out_10), .out_11(n10locationdata_1_out_11), .out_12(n10locationdata_1_out_12),
    .out_13(n10locationdata_1_out_13), .out_14(n10locationdata_1_out_14), .out_15(n10locationdata_1_out_15),
    .out_16(n10locationdata_1_out_16), .out_17(n10locationdata_1_out_17), .out_18(n10locationdata_1_out_18),
    .out_19(n10locationdata_1_out_19), .out_20(n10locationdata_1_out_20), .out_21(n10locationdata_1_out_21),
    .out_22(n10locationdata_1_out_22), .out_23(n10locationdata_1_out_23), .out_24(n10locationdata_1_out_24),
    .out_25(n10locationdata_1_out_25), .out_26(n10locationdata_1_out_26), .out_27(n10locationdata_1_out_27),
    .out_28(n10locationdata_1_out_28), .out_29(n10locationdata_1_out_29), .out_30(n10locationdata_1_out_30),
    .out_31(n10locationdata_1_out_31), .out_32(n10locationdata_1_out_32));
  Multiplexer #(.width(5), .enable("false")) multiplexer_2 (
    .in1(5'b00010), .out(X___start), .sel(On_Off));  // open: in0
  Level_Installer level_installer_1 (
    .Number_of_column(counter_2_q), .Column(level_installer_1_column), .bus_0(n10locationdata_1_out_1),
    .bus_1(n10locationdata_1_out_2), .bus_2(n10locationdata_1_out_3), .bus_3(n10locationdata_1_out_4),
    .bus_4(n10locationdata_1_out_5), .bus_5(n10locationdata_1_out_6), .bus_6(n10locationdata_1_out_7),
    .bus_7(n10locationdata_1_out_8), .bus_8(n10locationdata_1_out_9), .bus_9(n10locationdata_1_out_10),
    .bus_10(n10locationdata_1_out_11), .bus_11(n10locationdata_1_out_12), .bus_12(n10locationdata_1_out_13),
    .bus_13(n10locationdata_1_out_14), .bus_14(n10locationdata_1_out_15), .bus_15(n10locationdata_1_out_16),
    .bus_16(n10locationdata_1_out_17), .bus_17(n10locationdata_1_out_18), .bus_18(n10locationdata_1_out_19),
    .bus_19(n10locationdata_1_out_20), .bus_20(n10locationdata_1_out_21), .bus_21(n10locationdata_1_out_22),
    .bus_22(n10locationdata_1_out_23), .bus_23(n10locationdata_1_out_24), .bus_24(n10locationdata_1_out_25),
    .bus_25(n10locationdata_1_out_26), .bus_26(n10locationdata_1_out_27), .bus_27(n10locationdata_1_out_28),
    .bus_28(n10locationdata_1_out_29), .bus_29(n10locationdata_1_out_30), .bus_30(n10locationdata_1_out_31),
    .bus_31(n10locationdata_1_out_32));
  Multiplexer #(.width(32), .enable("false")) multiplexer_3 (
    .in1(level_installer_1_column), .out(Column), .sel(On_Off));  // open: in0
  Multiplexer #(.width(5), .enable("false")) multiplexer_4 (
    .in1(5'b00110), .out(Y___start), .sel(On_Off));  // open: in0
  Multiplexer #(.width(5), .enable("false")) multiplexer_5 (
    .in1(5'b01001), .out(X___finishTo), .sel(On_Off));  // open: in0
  Multiplexer #(.width(5), .enable("false")) multiplexer_6 (
    .in1({5{1'b1}}), .out(Y___finishTo), .sel(On_Off));  // open: in0
  Multiplexer #(.width(5), .enable("false")) multiplexer_7 (
    .in1(5'b00100), .out(X___finishFrom), .sel(On_Off));  // open: in0
  Multiplexer #(.width(5), .enable("false")) multiplexer_8 (
    .in1({5{1'b1}}), .out(Y___finishFrom), .sel(On_Off));  // open: in0

  // Other names for the same wires on the sheet: do = On_Off

  // Notes on the sheet:
  //   Level Loader
endmodule

module _10locationData (
  output [31:0] out_1,
  output [31:0] out_2,
  output [31:0] out_3,
  output [31:0] out_4,
  output [31:0] out_5,
  output [31:0] out_6,
  output [31:0] out_7,
  output [31:0] out_8,
  output [31:0] out_9,
  output [31:0] out_10,
  output [31:0] out_11,
  output [31:0] out_12,
  output [31:0] out_13,
  output [31:0] out_14,
  output [31:0] out_15,
  output [31:0] out_16,
  output [31:0] out_17,
  output [31:0] out_18,
  output [31:0] out_19,
  output [31:0] out_20,
  output [31:0] out_21,
  output [31:0] out_22,
  output [31:0] out_23,
  output [31:0] out_24,
  output [31:0] out_25,
  output [31:0] out_26,
  output [31:0] out_27,
  output [31:0] out_28,
  output [31:0] out_29,
  output [31:0] out_30,
  output [31:0] out_31,
  output [31:0] out_32
);


  assign out_1 = 32'hfffffe0f;
  assign out_2 = 32'h80000009;
  assign out_3 = 32'h80000009;
  assign out_4 = 32'h80000009;
  assign out_5 = 32'h9;
  assign out_6 = 32'h1;
  assign out_7 = 32'h8000001;
  assign out_8 = 32'h8000001;
  assign out_9 = 32'h1;
  assign out_10 = 32'h9;
  assign out_11 = 32'h82000001;
  assign out_12 = 32'h82000001;
  assign out_13 = 32'h80000001;
  assign out_14 = 32'h80000009;
  assign out_15 = 32'h80800009;
  assign out_16 = 32'h80841041;
  assign out_17 = 32'h80208241;
  assign out_18 = 32'h80000001;
  assign out_19 = 32'h80000001;
  assign out_20 = 32'h80000001;
  assign out_21 = 32'h80000001;
  assign out_22 = 32'h80000001;
  assign out_23 = 32'h80000001;
  assign out_24 = 32'h80000001;
  assign out_25 = 32'h80000001;
  assign out_26 = 32'h80000001;
  assign out_27 = 32'h80000001;
  assign out_28 = 32'h80000001;
  assign out_29 = 32'h80000001;
  assign out_30 = 32'h80000001;
  assign out_31 = 32'h80000001;
  assign out_32 = {32{1'b1}};
endmodule
